// Logisim project mycomputer_64.circ as structural Verilog: 20 circuits, main circuit main
module main (
  output [63:0] out_1
);

  wire clk, MemRead, MemWrite, not_1_out;
  wire [23:0] cpu_64_1_read;
  wire [63:0] MemWrite_Data, ram_1_dout;
  wire [63:24] cpu_64_1_read_2;

  Clock clock_1 (.out(clk));
  not not_1 (not_1_out, MemWrite);
  RAM #(.addrWidth(24), .asyncread("true"), .dataWidth(64), .trigger("falling")) ram_1 (
    .addr(cpu_64_1_read), .we(MemWrite), .oe(not_1_out), .clk(clk), .din(MemWrite_Data), .dout(ram_1_dout));
  CPU_64 cpu_64_1 (
    .in_1(ram_1_dout), .Clock(clk), .Read({cpu_64_1_read_2, cpu_64_1_read}), .CPU_out(out_1),
    .MemRead(MemRead), .MemWrite(MemWrite), .MemWrite_Data(MemWrite_Data));
endmodule

module FA (
  input  A,
  input  B,
  input  Cin,
  output Sum,
  output Cout
);

  wire AND1_out, AND2_out, XOR1_out;

  xor XOR1 (XOR1_out, A, B);
  and AND1 (AND1_out, A, B);
  xor XOR2 (Sum, XOR1_out, Cin);
  and AND2 (AND2_out, XOR1_out, Cin);
  or or_1 (Cout, AND1_out, AND2_out);
endmodule

module ADDER_64 (
  input  [63:0] A,
  input  [63:0] B,
  input  Cin,
  output [63:0] S,
  output S65
);

  wire [62:0] CC;

  FA fa_1 (.A(A[0]), .B(B[0]), .Cin(Cin), .Sum(S[0]), .Cout(CC[0]));
  FA fa_2 (.A(A[1]), .B(B[1]), .Cin(CC[0]), .Sum(S[1]), .Cout(CC[1]));
  FA fa_3 (.A(A[2]), .B(B[2]), .Cin(CC[1]), .Sum(S[2]), .Cout(CC[2]));
  FA fa_4 (.A(A[3]), .B(B[3]), .Cin(CC[2]), .Sum(S[3]), .Cout(CC[3]));
  FA fa_5 (.A(A[4]), .B(B[4]), .Cin(CC[3]), .Sum(S[4]), .Cout(CC[4]));
  FA fa_6 (.A(A[5]), .B(B[5]), .Cin(CC[4]), .Sum(S[5]), .Cout(CC[5]));
  FA fa_7 (.A(A[6]), .B(B[6]), .Cin(CC[5]), .Sum(S[6]), .Cout(CC[6]));
  FA fa_8 (.A(A[7]), .B(B[7]), .Cin(CC[6]), .Sum(S[7]), .Cout(CC[7]));
  FA fa_9 (.A(A[8]), .B(B[8]), .Cin(CC[7]), .Sum(S[8]), .Cout(CC[8]));
  FA fa_10 (.A(A[9]), .B(B[9]), .Cin(CC[8]), .Sum(S[9]), .Cout(CC[9]));
  FA fa_11 (.A(A[10]), .B(B[10]), .Cin(CC[9]), .Sum(S[10]), .Cout(CC[10]));
  FA fa_12 (.A(A[11]), .B(B[11]), .Cin(CC[10]), .Sum(S[11]), .Cout(CC[11]));
  FA fa_13 (.A(A[12]), .B(B[12]), .Cin(CC[11]), .Sum(S[12]), .Cout(CC[12]));
  FA fa_14 (.A(A[13]), .B(B[13]), .Cin(CC[12]), .Sum(S[13]), .Cout(CC[13]));
  FA fa_15 (.A(A[14]), .B(B[14]), .Cin(CC[13]), .Sum(S[14]), .Cout(CC[14]));
  FA fa_16 (.A(A[15]), .B(B[15]), .Cin(CC[14]), .Sum(S[15]), .Cout(CC[15]));
  FA fa_17 (.A(A[16]), .B(B[16]), .Cin(CC[15]), .Sum(S[16]), .Cout(CC[16]));
  FA fa_18 (.A(A[17]), .B(B[17]), .Cin(CC[16]), .Sum(S[17]), .Cout(CC[17]));
  FA fa_19 (.A(A[18]), .B(B[18]), .Cin(CC[17]), .Sum(S[18]), .Cout(CC[18]));
  FA fa_20 (.A(A[19]), .B(B[19]), .Cin(CC[18]), .Sum(S[19]), .Cout(CC[19]));
  FA fa_21 (.A(A[20]), .B(B[20]), .Cin(CC[19]), .Sum(S[20]), .Cout(CC[20]));
  FA fa_22 (.A(A[21]), .B(B[21]), .Cin(CC[20]), .Sum(S[21]), .Cout(CC[21]));
  FA fa_23 (.A(A[22]), .B(B[22]), .Cin(CC[21]), .Sum(S[22]), .Cout(CC[22]));
  FA fa_24 (.A(A[23]), .B(B[23]), .Cin(CC[22]), .Sum(S[23]), .Cout(CC[23]));
  FA fa_25 (.A(A[24]), .B(B[24]), .Cin(CC[23]), .Sum(S[24]), .Cout(CC[24]));
  FA fa_26 (.A(A[25]), .B(B[25]), .Cin(CC[24]), .Sum(S[25]), .Cout(CC[25]));
  FA fa_27 (.A(A[26]), .B(B[26]), .Cin(CC[25]), .Sum(S[26]), .Cout(CC[26]));
  FA fa_28 (.A(A[27]), .B(B[27]), .Cin(CC[26]), .Sum(S[27]), .Cout(CC[27]));
  FA fa_29 (.A(A[28]), .B(B[28]), .Cin(CC[27]), .Sum(S[28]), .Cout(CC[28]));
  FA fa_30 (.A(A[29]), .B(B[29]), .Cin(CC[28]), .Sum(S[29]), .Cout(CC[29]));
  FA fa_31 (.A(A[30]), .B(B[30]), .Cin(CC[29]), .Sum(S[30]), .Cout(CC[30]));
  FA fa_32 (.A(A[31]), .B(B[31]), .Cin(CC[30]), .Sum(S[31]), .Cout(CC[31]));
  FA fa_33 (.A(A[32]), .B(B[32]), .Cin(CC[31]), .Sum(S[32]), .Cout(CC[32]));
  FA fa_34 (.A(A[33]), .B(B[33]), .Cin(CC[32]), .Sum(S[33]), .Cout(CC[33]));
  FA fa_35 (.A(A[34]), .B(B[34]), .Cin(CC[33]), .Sum(S[34]), .Cout(CC[34]));
  FA fa_36 (.A(A[35]), .B(B[35]), .Cin(CC[34]), .Sum(S[35]), .Cout(CC[35]));
  FA fa_37 (.A(A[36]), .B(B[36]), .Cin(CC[35]), .Sum(S[36]), .Cout(CC[36]));
  FA fa_38 (.A(A[37]), .B(B[37]), .Cin(CC[36]), .Sum(S[37]), .Cout(CC[37]));
  FA fa_39 (.A(A[38]), .B(B[38]), .Cin(CC[37]), .Sum(S[38]), .Cout(CC[38]));
  FA fa_40 (.A(A[39]), .B(B[39]), .Cin(CC[38]), .Sum(S[39]), .Cout(CC[39]));
  FA fa_41 (.A(A[40]), .B(B[40]), .Cin(CC[39]), .Sum(S[40]), .Cout(CC[40]));
  FA fa_42 (.A(A[41]), .B(B[41]), .Cin(CC[40]), .Sum(S[41]), .Cout(CC[41]));
  FA fa_43 (.A(A[42]), .B(B[42]), .Cin(CC[41]), .Sum(S[42]), .Cout(CC[42]));
  FA fa_44 (.A(A[43]), .B(B[43]), .Cin(CC[42]), .Sum(S[43]), .Cout(CC[43]));
  FA fa_45 (.A(A[44]), .B(B[44]), .Cin(CC[43]), .Sum(S[44]), .Cout(CC[44]));
  FA fa_46 (.A(A[45]), .B(B[45]), .Cin(CC[44]), .Sum(S[45]), .Cout(CC[45]));
  FA fa_47 (.A(A[46]), .B(B[46]), .Cin(CC[45]), .Sum(S[46]), .Cout(CC[46]));
  FA fa_48 (.A(A[47]), .B(B[47]), .Cin(CC[46]), .Sum(S[47]), .Cout(CC[47]));
  FA fa_49 (.A(A[48]), .B(B[48]), .Cin(CC[47]), .Sum(S[48]), .Cout(CC[48]));
  FA fa_50 (.A(A[49]), .B(B[49]), .Cin(CC[48]), .Sum(S[49]), .Cout(CC[49]));
  FA fa_51 (.A(A[50]), .B(B[50]), .Cin(CC[49]), .Sum(S[50]), .Cout(CC[50]));
  FA fa_52 (.A(A[51]), .B(B[51]), .Cin(CC[50]), .Sum(S[51]), .Cout(CC[51]));
  FA fa_53 (.A(A[52]), .B(B[52]), .Cin(CC[51]), .Sum(S[52]), .Cout(CC[52]));
  FA fa_54 (.A(A[53]), .B(B[53]), .Cin(CC[52]), .Sum(S[53]), .Cout(CC[53]));
  FA fa_55 (.A(A[54]), .B(B[54]), .Cin(CC[53]), .Sum(S[54]), .Cout(CC[54]));
  FA fa_56 (.A(A[55]), .B(B[55]), .Cin(CC[54]), .Sum(S[55]), .Cout(CC[55]));
  FA fa_57 (.A(A[56]), .B(B[56]), .Cin(CC[55]), .Sum(S[56]), .Cout(CC[56]));
  FA fa_58 (.A(A[57]), .B(B[57]), .Cin(CC[56]), .Sum(S[57]), .Cout(CC[57]));
  FA fa_59 (.A(A[58]), .B(B[58]), .Cin(CC[57]), .Sum(S[58]), .Cout(CC[58]));
  FA fa_60 (.A(A[59]), .B(B[59]), .Cin(CC[58]), .Sum(S[59]), .Cout(CC[59]));
  FA fa_61 (.A(A[60]), .B(B[60]), .Cin(CC[59]), .Sum(S[60]), .Cout(CC[60]));
  FA fa_62 (.A(A[61]), .B(B[61]), .Cin(CC[60]), .Sum(S[61]), .Cout(CC[61]));
  FA fa_63 (.A(A[62]), .B(B[62]), .Cin(CC[61]), .Sum(S[62]), .Cout(CC[62]));
  FA fa_64 (.A(A[63]), .B(B[63]), .Cin(CC[62]), .Sum(S[63]), .Cout(S65));
endmodule

module SUBTRACTOR_64 (
  input  [63:0] A,
  input  [63:0] B,
  output [63:0] diff,
  output Borrow
);

  wire adder_64_1_s65;
  wire [63:0] not_1_out;

  assign not_1_out = ~B;  // NOT_Gate not_1, 64 bits wide
  ADDER_64 adder_64_1 (.A(A), .B(not_1_out), .Cin(1'b1), .S(diff), .S65(adder_64_1_s65));
  not not_2 (Borrow, adder_64_1_s65);
endmodule

module AND_64 (
  input  [63:0] in_1,
  input  [63:0] in_2,
  output [63:0] out_3
);

  and and_1 (out_3[0], in_1[0], in_2[0]);
  and and_2 (out_3[1], in_1[1], in_2[1]);
  and and_3 (out_3[2], in_1[2], in_2[2]);
  and and_4 (out_3[3], in_1[3], in_2[3]);
  and and_5 (out_3[4], in_1[4], in_2[4]);
  and and_6 (out_3[5], in_1[5], in_2[5]);
  and and_7 (out_3[6], in_1[6], in_2[6]);
  and and_8 (out_3[7], in_1[7], in_2[7]);
  and and_9 (out_3[8], in_1[8], in_2[8]);
  and and_10 (out_3[9], in_1[9], in_2[9]);
  and and_11 (out_3[10], in_1[10], in_2[10]);
  and and_12 (out_3[11], in_1[11], in_2[11]);
  and and_13 (out_3[12], in_1[12], in_2[12]);
  and and_14 (out_3[13], in_1[13], in_2[13]);
  and and_15 (out_3[14], in_1[14], in_2[14]);
  and and_16 (out_3[15], in_1[15], in_2[15]);
  and and_17 (out_3[16], in_1[16], in_2[16]);
  and and_18 (out_3[17], in_1[17], in_2[17]);
  and and_19 (out_3[18], in_1[18], in_2[18]);
  and and_20 (out_3[19], in_1[19], in_2[19]);
  and and_21 (out_3[20], in_1[20], in_2[20]);
  and and_22 (out_3[21], in_1[21], in_2[21]);
  and and_23 (out_3[22], in_1[22], in_2[22]);
  and and_24 (out_3[23], in_1[23], in_2[23]);
  and and_25 (out_3[24], in_1[24], in_2[24]);
  and and_26 (out_3[25], in_1[25], in_2[25]);
  and and_27 (out_3[26], in_1[26], in_2[26]);
  and and_28 (out_3[27], in_1[27], in_2[27]);
  and and_29 (out_3[28], in_1[28], in_2[28]);
  and and_30 (out_3[29], in_1[29], in_2[29]);
  and and_31 (out_3[30], in_1[30], in_2[30]);
  and and_32 (out_3[31], in_1[31], in_2[31]);
  and and_33 (out_3[32], in_1[32], in_2[32]);
  and and_34 (out_3[33], in_1[33], in_2[33]);
  and and_35 (out_3[34], in_1[34], in_2[34]);
  and and_36 (out_3[35], in_1[35], in_2[35]);
  and and_37 (out_3[36], in_1[36], in_2[36]);
  and and_38 (out_3[37], in_1[37], in_2[37]);
  and and_39 (out_3[38], in_1[38], in_2[38]);
  and and_40 (out_3[39], in_1[39], in_2[39]);
  and and_41 (out_3[40], in_1[40], in_2[40]);
  and and_42 (out_3[41], in_1[41], in_2[41]);
  and and_43 (out_3[42], in_1[42], in_2[42]);
  and and_44 (out_3[43], in_1[43], in_2[43]);
  and and_45 (out_3[44], in_1[44], in_2[44]);
  and and_46 (out_3[45], in_1[45], in_2[45]);
  and and_47 (out_3[46], in_1[46], in_2[46]);
  and and_48 (out_3[47], in_1[47], in_2[47]);
  and and_49 (out_3[48], in_1[48], in_2[48]);
  and and_50 (out_3[49], in_1[49], in_2[49]);
  and and_51 (out_3[50], in_1[50], in_2[50]);
  and and_52 (out_3[51], in_1[51], in_2[51]);
  and and_53 (out_3[52], in_1[52], in_2[52]);
  and and_54 (out_3[53], in_1[53], in_2[53]);
  and and_55 (out_3[54], in_1[54], in_2[54]);
  and and_56 (out_3[55], in_1[55], in_2[55]);
  and and_57 (out_3[56], in_1[56], in_2[56]);
  and and_58 (out_3[57], in_1[57], in_2[57]);
  and and_59 (out_3[58], in_1[58], in_2[58]);
  and and_60 (out_3[59], in_1[59], in_2[59]);
  and and_61 (out_3[60], in_1[60], in_2[60]);
  and and_62 (out_3[61], in_1[61], in_2[61]);
  and and_63 (out_3[62], in_1[62], in_2[62]);
  and and_64 (out_3[63], in_1[63], in_2[63]);
endmodule

module OR_64 (
  input  [63:0] in_1,
  input  [63:0] in_2,
  output [63:0] out_3
);

  or or_1 (out_3[0], in_1[0], in_2[0]);
  or or_2 (out_3[1], in_1[1], in_2[1]);
  or or_3 (out_3[2], in_1[2], in_2[2]);
  or or_4 (out_3[3], in_1[3], in_2[3]);
  or or_5 (out_3[4], in_1[4], in_2[4]);
  or or_6 (out_3[5], in_1[5], in_2[5]);
  or or_7 (out_3[6], in_1[6], in_2[6]);
  or or_8 (out_3[7], in_1[7], in_2[7]);
  or or_9 (out_3[8], in_1[8], in_2[8]);
  or or_10 (out_3[9], in_1[9], in_2[9]);
  or or_11 (out_3[10], in_1[10], in_2[10]);
  or or_12 (out_3[11], in_1[11], in_2[11]);
  or or_13 (out_3[12], in_1[12], in_2[12]);
  or or_14 (out_3[13], in_1[13], in_2[13]);
  or or_15 (out_3[14], in_1[14], in_2[14]);
  or or_16 (out_3[15], in_1[15], in_2[15]);
  or or_17 (out_3[16], in_1[16], in_2[16]);
  or or_18 (out_3[17], in_1[17], in_2[17]);
  or or_19 (out_3[18], in_1[18], in_2[18]);
  or or_20 (out_3[19], in_1[19], in_2[19]);
  or or_21 (out_3[20], in_1[20], in_2[20]);
  or or_22 (out_3[21], in_1[21], in_2[21]);
  or or_23 (out_3[22], in_1[22], in_2[22]);
  or or_24 (out_3[23], in_1[23], in_2[23]);
  or or_25 (out_3[24], in_1[24], in_2[24]);
  or or_26 (out_3[25], in_1[25], in_2[25]);
  or or_27 (out_3[26], in_1[26], in_2[26]);
  or or_28 (out_3[27], in_1[27], in_2[27]);
  or or_29 (out_3[28], in_1[28], in_2[28]);
  or or_30 (out_3[29], in_1[29], in_2[29]);
  or or_31 (out_3[30], in_1[30], in_2[30]);
  or or_32 (out_3[31], in_1[31], in_2[31]);
  or or_33 (out_3[32], in_1[32], in_2[32]);
  or or_34 (out_3[33], in_1[33], in_2[33]);
  or or_35 (out_3[34], in_1[34], in_2[34]);
  or or_36 (out_3[35], in_1[35], in_2[35]);
  or or_37 (out_3[36], in_1[36], in_2[36]);
  or or_38 (out_3[37], in_1[37], in_2[37]);
  or or_39 (out_3[38], in_1[38], in_2[38]);
  or or_40 (out_3[39], in_1[39], in_2[39]);
  or or_41 (out_3[40], in_1[40], in_2[40]);
  or or_42 (out_3[41], in_1[41], in_2[41]);
  or or_43 (out_3[42], in_1[42], in_2[42]);
  or or_44 (out_3[43], in_1[43], in_2[43]);
  or or_45 (out_3[44], in_1[44], in_2[44]);
  or or_46 (out_3[45], in_1[45], in_2[45]);
  or or_47 (out_3[46], in_1[46], in_2[46]);
  or or_48 (out_3[47], in_1[47], in_2[47]);
  or or_49 (out_3[48], in_1[48], in_2[48]);
  or or_50 (out_3[49], in_1[49], in_2[49]);
  or or_51 (out_3[50], in_1[50], in_2[50]);
  or or_52 (out_3[51], in_1[51], in_2[51]);
  or or_53 (out_3[52], in_1[52], in_2[52]);
  or or_54 (out_3[53], in_1[53], in_2[53]);
  or or_55 (out_3[54], in_1[54], in_2[54]);
  or or_56 (out_3[55], in_1[55], in_2[55]);
  or or_57 (out_3[56], in_1[56], in_2[56]);
  or or_58 (out_3[57], in_1[57], in_2[57]);
  or or_59 (out_3[58], in_1[58], in_2[58]);
  or or_60 (out_3[59], in_1[59], in_2[59]);
  or or_61 (out_3[60], in_1[60], in_2[60]);
  or or_62 (out_3[61], in_1[61], in_2[61]);
  or or_63 (out_3[62], in_1[62], in_2[62]);
  or or_64 (out_3[63], in_1[63], in_2[63]);
endmodule

module ALU_64 (
  input  [63:0] A,
  input  [63:0] B,
  input  [1:0] OP,
  input  LDA,
  output Borrow,
  output [63:0] R
);

  wire [63:0] AN, DIFF, multiplexer_2_out, RO, S;

  ADDER_64 adder_64_1 (.A(A), .B(B), .Cin(1'b0), .S(S));  // open: S65
  SUBTRACTOR_64 subtractor_64_1 (.A(A), .B(B), .diff(DIFF), .Borrow(Borrow));
  AND_64 and_64_1 (.in_1(A), .in_2(B), .out_3(AN));
  OR_64 or_64_1 (.in_1(A), .in_2(B), .out_3(RO));
  Multiplexer #(.width(64)) multiplexer_1 (.in0(multiplexer_2_out), .in1(B), .out(R), .sel(LDA));
  Multiplexer #(.select(2), .width(64)) multiplexer_2 (
    .in0(S), .in1(DIFF), .in2(AN), .in3(RO), .out(multiplexer_2_out), .sel(OP));
endmodule

module REG_64 (
  input  [63:0] D,
  input  Clock,
  output [63:0] Q
);

  D_Flip_Flop #(.trigger("falling")) d_ff_1 (.D(D[0]), .clk(Clock), .Q(Q[0]), .preset(1'b0), .reset(1'b0));  // open: Qn
  D_Flip_Flop #(.trigger("falling")) d_ff_2 (.D(D[1]), .clk(Clock), .Q(Q[1]), .preset(1'b0), .reset(1'b0));  // open: Qn
  D_Flip_Flop #(.trigger("falling")) d_ff_3 (.D(D[2]), .clk(Clock), .Q(Q[2]), .preset(1'b0), .reset(1'b0));  // open: Qn
  D_Flip_Flop #(.trigger("falling")) d_ff_4 (.D(D[3]), .clk(Clock), .Q(Q[3]), .preset(1'b0), .reset(1'b0));  // open: Qn
  D_Flip_Flop #(.trigger("falling")) d_ff_5 (.D(D[4]), .clk(Clock), .Q(Q[4]), .preset(1'b0), .reset(1'b0));  // open: Qn
  D_Flip_Flop #(.trigger("falling")) d_ff_6 (.D(D[5]), .clk(Clock), .Q(Q[5]), .preset(1'b0), .reset(1'b0));  // open: Qn
  D_Flip_Flop #(.trigger("falling")) d_ff_7 (.D(D[6]), .clk(Clock), .Q(Q[6]), .preset(1'b0), .reset(1'b0));  // open: Qn
  D_Flip_Flop #(.trigger("falling")) d_ff_8 (.D(D[7]), .clk(Clock), .Q(Q[7]), .preset(1'b0), .reset(1'b0));  // open: Qn
  D_Flip_Flop #(.trigger("falling")) d_ff_9 (.D(D[8]), .clk(Clock), .Q(Q[8]), .preset(1'b0), .reset(1'b0));  // open: Qn
  D_Flip_Flop #(.trigger("falling")) d_ff_10 (
    .D(D[9]), .clk(Clock), .Q(Q[9]), .preset(1'b0), .reset(1'b0));  // open: Qn
  D_Flip_Flop #(.trigger("falling")) d_ff_11 (
    .D(D[10]), .clk(Clock), .Q(Q[10]), .preset(1'b0), .reset(1'b0));  // open: Qn
  D_Flip_Flop #(.trigger("falling")) d_ff_12 (
    .D(D[11]), .clk(Clock), .Q(Q[11]), .preset(1'b0), .reset(1'b0));  // open: Qn
  D_Flip_Flop #(.trigger("falling")) d_ff_13 (
    .D(D[12]), .clk(Clock), .Q(Q[12]), .preset(1'b0), .reset(1'b0));  // open: Qn
  D_Flip_Flop #(.trigger("falling")) d_ff_14 (
    .D(D[13]), .clk(Clock), .Q(Q[13]), .preset(1'b0), .reset(1'b0));  // open: Qn
  D_Flip_Flop #(.trigger("falling")) d_ff_15 (
    .D(D[14]), .clk(Clock), .Q(Q[14]), .preset(1'b0), .reset(1'b0));  // open: Qn
  D_Flip_Flop #(.trigger("falling")) d_ff_16 (
    .D(D[15]), .clk(Clock), .Q(Q[15]), .preset(1'b0), .reset(1'b0));  // open: Qn
  D_Flip_Flop #(.trigger("falling")) d_ff_17 (
    .D(D[16]), .clk(Clock), .Q(Q[16]), .preset(1'b0), .reset(1'b0));  // open: Qn
  D_Flip_Flop #(.trigger("falling")) d_ff_18 (
    .D(D[17]), .clk(Clock), .Q(Q[17]), .preset(1'b0), .reset(1'b0));  // open: Qn
  D_Flip_Flop #(.trigger("falling")) d_ff_19 (
    .D(D[18]), .clk(Clock), .Q(Q[18]), .preset(1'b0), .reset(1'b0));  // open: Qn
  D_Flip_Flop #(.trigger("falling")) d_ff_20 (
    .D(D[19]), .clk(Clock), .Q(Q[19]), .preset(1'b0), .reset(1'b0));  // open: Qn
  D_Flip_Flop #(.trigger("falling")) d_ff_21 (
    .D(D[20]), .clk(Clock), .Q(Q[20]), .preset(1'b0), .reset(1'b0));  // open: Qn
  D_Flip_Flop #(.trigger("falling")) d_ff_22 (
    .D(D[21]), .clk(Clock), .Q(Q[21]), .preset(1'b0), .reset(1'b0));  // open: Qn
  D_Flip_Flop #(.trigger("falling")) d_ff_23 (
    .D(D[22]), .clk(Clock), .Q(Q[22]), .preset(1'b0), .reset(1'b0));  // open: Qn
  D_Flip_Flop #(.trigger("falling")) d_ff_24 (
    .D(D[23]), .clk(Clock), .Q(Q[23]), .preset(1'b0), .reset(1'b0));  // open: Qn
  D_Flip_Flop #(.trigger("falling")) d_ff_25 (
    .D(D[24]), .clk(Clock), .Q(Q[24]), .preset(1'b0), .reset(1'b0));  // open: Qn
  D_Flip_Flop #(.trigger("falling")) d_ff_26 (
    .D(D[25]), .clk(Clock), .Q(Q[25]), .preset(1'b0), .reset(1'b0));  // open: Qn
  D_Flip_Flop #(.trigger("falling")) d_ff_27 (
    .D(D[26]), .clk(Clock), .Q(Q[26]), .preset(1'b0), .reset(1'b0));  // open: Qn
  D_Flip_Flop #(.trigger("falling")) d_ff_28 (
    .D(D[27]), .clk(Clock), .Q(Q[27]), .preset(1'b0), .reset(1'b0));  // open: Qn
  D_Flip_Flop #(.trigger("falling")) d_ff_29 (
    .D(D[28]), .clk(Clock), .Q(Q[28]), .preset(1'b0), .reset(1'b0));  // open: Qn
  D_Flip_Flop #(.trigger("falling")) d_ff_30 (
    .D(D[29]), .clk(Clock), .Q(Q[29]), .preset(1'b0), .reset(1'b0));  // open: Qn
  D_Flip_Flop #(.trigger("falling")) d_ff_31 (
    .D(D[30]), .clk(Clock), .Q(Q[30]), .preset(1'b0), .reset(1'b0));  // open: Qn
  D_Flip_Flop #(.trigger("falling")) d_ff_32 (
    .D(D[31]), .clk(Clock), .Q(Q[31]), .preset(1'b0), .reset(1'b0));  // open: Qn
  D_Flip_Flop #(.trigger("falling")) d_ff_33 (
    .D(D[32]), .clk(Clock), .Q(Q[32]), .preset(1'b0), .reset(1'b0));  // open: Qn
  D_Flip_Flop #(.trigger("falling")) d_ff_34 (
    .D(D[33]), .clk(Clock), .Q(Q[33]), .preset(1'b0), .reset(1'b0));  // open: Qn
  D_Flip_Flop #(.trigger("falling")) d_ff_35 (
    .D(D[34]), .clk(Clock), .Q(Q[34]), .preset(1'b0), .reset(1'b0));  // open: Qn
  D_Flip_Flop #(.trigger("falling")) d_ff_36 (
    .D(D[35]), .clk(Clock), .Q(Q[35]), .preset(1'b0), .reset(1'b0));  // open: Qn
  D_Flip_Flop #(.trigger("falling")) d_ff_37 (
    .D(D[36]), .clk(Clock), .Q(Q[36]), .preset(1'b0), .reset(1'b0));  // open: Qn
  D_Flip_Flop #(.trigger("falling")) d_ff_38 (
    .D(D[37]), .clk(Clock), .Q(Q[37]), .preset(1'b0), .reset(1'b0));  // open: Qn
  D_Flip_Flop #(.trigger("falling")) d_ff_39 (
    .D(D[38]), .clk(Clock), .Q(Q[38]), .preset(1'b0), .reset(1'b0));  // open: Qn
  D_Flip_Flop #(.trigger("falling")) d_ff_40 (
    .D(D[39]), .clk(Clock), .Q(Q[39]), .preset(1'b0), .reset(1'b0));  // open: Qn
  D_Flip_Flop #(.trigger("falling")) d_ff_41 (
    .D(D[40]), .clk(Clock), .Q(Q[40]), .preset(1'b0), .reset(1'b0));  // open: Qn
  D_Flip_Flop #(.trigger("falling")) d_ff_42 (
    .D(D[41]), .clk(Clock), .Q(Q[41]), .preset(1'b0), .reset(1'b0));  // open: Qn
  D_Flip_Flop #(.trigger("falling")) d_ff_43 (
    .D(D[42]), .clk(Clock), .Q(Q[42]), .preset(1'b0), .reset(1'b0));  // open: Qn
  D_Flip_Flop #(.trigger("falling")) d_ff_44 (
    .D(D[43]), .clk(Clock), .Q(Q[43]), .preset(1'b0), .reset(1'b0));  // open: Qn
  D_Flip_Flop #(.trigger("falling")) d_ff_45 (
    .D(D[44]), .clk(Clock), .Q(Q[44]), .preset(1'b0), .reset(1'b0));  // open: Qn
  D_Flip_Flop #(.trigger("falling")) d_ff_46 (
    .D(D[45]), .clk(Clock), .Q(Q[45]), .preset(1'b0), .reset(1'b0));  // open: Qn
  D_Flip_Flop #(.trigger("falling")) d_ff_47 (
    .D(D[46]), .clk(Clock), .Q(Q[46]), .preset(1'b0), .reset(1'b0));  // open: Qn
  D_Flip_Flop #(.trigger("falling")) d_ff_48 (
    .D(D[47]), .clk(Clock), .Q(Q[47]), .preset(1'b0), .reset(1'b0));  // open: Qn
  D_Flip_Flop #(.trigger("falling")) d_ff_49 (
    .D(D[48]), .clk(Clock), .Q(Q[48]), .preset(1'b0), .reset(1'b0));  // open: Qn
  D_Flip_Flop #(.trigger("falling")) d_ff_50 (
    .D(D[49]), .clk(Clock), .Q(Q[49]), .preset(1'b0), .reset(1'b0));  // open: Qn
  D_Flip_Flop #(.trigger("falling")) d_ff_51 (
    .D(D[50]), .clk(Clock), .Q(Q[50]), .preset(1'b0), .reset(1'b0));  // open: Qn
  D_Flip_Flop #(.trigger("falling")) d_ff_52 (
    .D(D[51]), .clk(Clock), .Q(Q[51]), .preset(1'b0), .reset(1'b0));  // open: Qn
  D_Flip_Flop #(.trigger("falling")) d_ff_53 (
    .D(D[52]), .clk(Clock), .Q(Q[52]), .preset(1'b0), .reset(1'b0));  // open: Qn
  D_Flip_Flop #(.trigger("falling")) d_ff_54 (
    .D(D[53]), .clk(Clock), .Q(Q[53]), .preset(1'b0), .reset(1'b0));  // open: Qn
  D_Flip_Flop #(.trigger("falling")) d_ff_55 (
    .D(D[54]), .clk(Clock), .Q(Q[54]), .preset(1'b0), .reset(1'b0));  // open: Qn
  D_Flip_Flop #(.trigger("falling")) d_ff_56 (
    .D(D[55]), .clk(Clock), .Q(Q[55]), .preset(1'b0), .reset(1'b0));  // open: Qn
  D_Flip_Flop #(.trigger("falling")) d_ff_57 (
    .D(D[56]), .clk(Clock), .Q(Q[56]), .preset(1'b0), .reset(1'b0));  // open: Qn
  D_Flip_Flop #(.trigger("falling")) d_ff_58 (
    .D(D[57]), .clk(Clock), .Q(Q[57]), .preset(1'b0), .reset(1'b0));  // open: Qn
  D_Flip_Flop #(.trigger("falling")) d_ff_59 (
    .D(D[58]), .clk(Clock), .Q(Q[58]), .preset(1'b0), .reset(1'b0));  // open: Qn
  D_Flip_Flop #(.trigger("falling")) d_ff_60 (
    .D(D[59]), .clk(Clock), .Q(Q[59]), .preset(1'b0), .reset(1'b0));  // open: Qn
  D_Flip_Flop #(.trigger("falling")) d_ff_61 (
    .D(D[60]), .clk(Clock), .Q(Q[60]), .preset(1'b0), .reset(1'b0));  // open: Qn
  D_Flip_Flop #(.trigger("falling")) d_ff_62 (
    .D(D[61]), .clk(Clock), .Q(Q[61]), .preset(1'b0), .reset(1'b0));  // open: Qn
  D_Flip_Flop #(.trigger("falling")) d_ff_63 (
    .D(D[62]), .clk(Clock), .Q(Q[62]), .preset(1'b0), .reset(1'b0));  // open: Qn
  D_Flip_Flop #(.trigger("falling")) d_ff_64 (
    .D(D[63]), .clk(Clock), .Q(Q[63]), .preset(1'b0), .reset(1'b0));  // open: Qn
endmodule

module IR_64 (
  input  [63:0] D,
  input  Clock,
  output [63:0] Q
);

  D_Flip_Flop #(.trigger("falling")) d_ff_1 (.D(D[0]), .clk(Clock), .Q(Q[0]), .preset(1'b0), .reset(1'b0));  // open: Qn
  D_Flip_Flop #(.trigger("falling")) d_ff_2 (.D(D[1]), .clk(Clock), .Q(Q[1]), .preset(1'b0), .reset(1'b0));  // open: Qn
  D_Flip_Flop #(.trigger("falling")) d_ff_3 (.D(D[2]), .clk(Clock), .Q(Q[2]), .preset(1'b0), .reset(1'b0));  // open: Qn
  D_Flip_Flop #(.trigger("falling")) d_ff_4 (.D(D[3]), .clk(Clock), .Q(Q[3]), .preset(1'b0), .reset(1'b0));  // open: Qn
  D_Flip_Flop #(.trigger("falling")) d_ff_5 (.D(D[4]), .clk(Clock), .Q(Q[4]), .preset(1'b0), .reset(1'b0));  // open: Qn
  D_Flip_Flop #(.trigger("falling")) d_ff_6 (.D(D[5]), .clk(Clock), .Q(Q[5]), .preset(1'b0), .reset(1'b0));  // open: Qn
  D_Flip_Flop #(.trigger("falling")) d_ff_7 (.D(D[6]), .clk(Clock), .Q(Q[6]), .preset(1'b0), .reset(1'b0));  // open: Qn
  D_Flip_Flop #(.trigger("falling")) d_ff_8 (.D(D[7]), .clk(Clock), .Q(Q[7]), .preset(1'b0), .reset(1'b0));  // open: Qn
  D_Flip_Flop #(.trigger("falling")) d_ff_9 (.D(D[8]), .clk(Clock), .Q(Q[8]), .preset(1'b0), .reset(1'b0));  // open: Qn
  D_Flip_Flop #(.trigger("falling")) d_ff_10 (
    .D(D[9]), .clk(Clock), .Q(Q[9]), .preset(1'b0), .reset(1'b0));  // open: Qn
  D_Flip_Flop #(.trigger("falling")) d_ff_11 (
    .D(D[10]), .clk(Clock), .Q(Q[10]), .preset(1'b0), .reset(1'b0));  // open: Qn
  D_Flip_Flop #(.trigger("falling")) d_ff_12 (
    .D(D[11]), .clk(Clock), .Q(Q[11]), .preset(1'b0), .reset(1'b0));  // open: Qn
  D_Flip_Flop #(.trigger("falling")) d_ff_13 (
    .D(D[12]), .clk(Clock), .Q(Q[12]), .preset(1'b0), .reset(1'b0));  // open: Qn
  D_Flip_Flop #(.trigger("falling")) d_ff_14 (
    .D(D[13]), .clk(Clock), .Q(Q[13]), .preset(1'b0), .reset(1'b0));  // open: Qn
  D_Flip_Flop #(.trigger("falling")) d_ff_15 (
    .D(D[14]), .clk(Clock), .Q(Q[14]), .preset(1'b0), .reset(1'b0));  // open: Qn
  D_Flip_Flop #(.trigger("falling")) d_ff_16 (
    .D(D[15]), .clk(Clock), .Q(Q[15]), .preset(1'b0), .reset(1'b0));  // open: Qn
  D_Flip_Flop #(.trigger("falling")) d_ff_17 (
    .D(D[16]), .clk(Clock), .Q(Q[16]), .preset(1'b0), .reset(1'b0));  // open: Qn
  D_Flip_Flop #(.trigger("falling")) d_ff_18 (
    .D(D[17]), .clk(Clock), .Q(Q[17]), .preset(1'b0), .reset(1'b0));  // open: Qn
  D_Flip_Flop #(.trigger("falling")) d_ff_19 (
    .D(D[18]), .clk(Clock), .Q(Q[18]), .preset(1'b0), .reset(1'b0));  // open: Qn
  D_Flip_Flop #(.trigger("falling")) d_ff_20 (
    .D(D[19]), .clk(Clock), .Q(Q[19]), .preset(1'b0), .reset(1'b0));  // open: Qn
  D_Flip_Flop #(.trigger("falling")) d_ff_21 (
    .D(D[20]), .clk(Clock), .Q(Q[20]), .preset(1'b0), .reset(1'b0));  // open: Qn
  D_Flip_Flop #(.trigger("falling")) d_ff_22 (
    .D(D[21]), .clk(Clock), .Q(Q[21]), .preset(1'b0), .reset(1'b0));  // open: Qn
  D_Flip_Flop #(.trigger("falling")) d_ff_23 (
    .D(D[22]), .clk(Clock), .Q(Q[22]), .preset(1'b0), .reset(1'b0));  // open: Qn
  D_Flip_Flop #(.trigger("falling")) d_ff_24 (
    .D(D[23]), .clk(Clock), .Q(Q[23]), .preset(1'b0), .reset(1'b0));  // open: Qn
  D_Flip_Flop #(.trigger("falling")) d_ff_25 (
    .D(D[24]), .clk(Clock), .Q(Q[24]), .preset(1'b0), .reset(1'b0));  // open: Qn
  D_Flip_Flop #(.trigger("falling")) d_ff_26 (
    .D(D[25]), .clk(Clock), .Q(Q[25]), .preset(1'b0), .reset(1'b0));  // open: Qn
  D_Flip_Flop #(.trigger("falling")) d_ff_27 (
    .D(D[26]), .clk(Clock), .Q(Q[26]), .preset(1'b0), .reset(1'b0));  // open: Qn
  D_Flip_Flop #(.trigger("falling")) d_ff_28 (
    .D(D[27]), .clk(Clock), .Q(Q[27]), .preset(1'b0), .reset(1'b0));  // open: Qn
  D_Flip_Flop #(.trigger("falling")) d_ff_29 (
    .D(D[28]), .clk(Clock), .Q(Q[28]), .preset(1'b0), .reset(1'b0));  // open: Qn
  D_Flip_Flop #(.trigger("falling")) d_ff_30 (
    .D(D[29]), .clk(Clock), .Q(Q[29]), .preset(1'b0), .reset(1'b0));  // open: Qn
  D_Flip_Flop #(.trigger("falling")) d_ff_31 (
    .D(D[30]), .clk(Clock), .Q(Q[30]), .preset(1'b0), .reset(1'b0));  // open: Qn
  D_Flip_Flop #(.trigger("falling")) d_ff_32 (
    .D(D[31]), .clk(Clock), .Q(Q[31]), .preset(1'b0), .reset(1'b0));  // open: Qn
  D_Flip_Flop #(.trigger("falling")) d_ff_33 (
    .D(D[32]), .clk(Clock), .Q(Q[32]), .preset(1'b0), .reset(1'b0));  // open: Qn
  D_Flip_Flop #(.trigger("falling")) d_ff_34 (
    .D(D[33]), .clk(Clock), .Q(Q[33]), .preset(1'b0), .reset(1'b0));  // open: Qn
  D_Flip_Flop #(.trigger("falling")) d_ff_35 (
    .D(D[34]), .clk(Clock), .Q(Q[34]), .preset(1'b0), .reset(1'b0));  // open: Qn
  D_Flip_Flop #(.trigger("falling")) d_ff_36 (
    .D(D[35]), .clk(Clock), .Q(Q[35]), .preset(1'b0), .reset(1'b0));  // open: Qn
  D_Flip_Flop #(.trigger("falling")) d_ff_37 (
    .D(D[36]), .clk(Clock), .Q(Q[36]), .preset(1'b0), .reset(1'b0));  // open: Qn
  D_Flip_Flop #(.trigger("falling")) d_ff_38 (
    .D(D[37]), .clk(Clock), .Q(Q[37]), .preset(1'b0), .reset(1'b0));  // open: Qn
  D_Flip_Flop #(.trigger("falling")) d_ff_39 (
    .D(D[38]), .clk(Clock), .Q(Q[38]), .preset(1'b0), .reset(1'b0));  // open: Qn
  D_Flip_Flop #(.trigger("falling")) d_ff_40 (
    .D(D[39]), .clk(Clock), .Q(Q[39]), .preset(1'b0), .reset(1'b0));  // open: Qn
  D_Flip_Flop #(.trigger("falling")) d_ff_41 (
    .D(D[40]), .clk(Clock), .Q(Q[40]), .preset(1'b0), .reset(1'b0));  // open: Qn
  D_Flip_Flop #(.trigger("falling")) d_ff_42 (
    .D(D[41]), .clk(Clock), .Q(Q[41]), .preset(1'b0), .reset(1'b0));  // open: Qn
  D_Flip_Flop #(.trigger("falling")) d_ff_43 (
    .D(D[42]), .clk(Clock), .Q(Q[42]), .preset(1'b0), .reset(1'b0));  // open: Qn
  D_Flip_Flop #(.trigger("falling")) d_ff_44 (
    .D(D[43]), .clk(Clock), .Q(Q[43]), .preset(1'b0), .reset(1'b0));  // open: Qn
  D_Flip_Flop #(.trigger("falling")) d_ff_45 (
    .D(D[44]), .clk(Clock), .Q(Q[44]), .preset(1'b0), .reset(1'b0));  // open: Qn
  D_Flip_Flop #(.trigger("falling")) d_ff_46 (
    .D(D[45]), .clk(Clock), .Q(Q[45]), .preset(1'b0), .reset(1'b0));  // open: Qn
  D_Flip_Flop #(.trigger("falling")) d_ff_47 (
    .D(D[46]), .clk(Clock), .Q(Q[46]), .preset(1'b0), .reset(1'b0));  // open: Qn
  D_Flip_Flop #(.trigger("falling")) d_ff_48 (
    .D(D[47]), .clk(Clock), .Q(Q[47]), .preset(1'b0), .reset(1'b0));  // open: Qn
  D_Flip_Flop #(.trigger("falling")) d_ff_49 (
    .D(D[48]), .clk(Clock), .Q(Q[48]), .preset(1'b0), .reset(1'b0));  // open: Qn
  D_Flip_Flop #(.trigger("falling")) d_ff_50 (
    .D(D[49]), .clk(Clock), .Q(Q[49]), .preset(1'b0), .reset(1'b0));  // open: Qn
  D_Flip_Flop #(.trigger("falling")) d_ff_51 (
    .D(D[50]), .clk(Clock), .Q(Q[50]), .preset(1'b0), .reset(1'b0));  // open: Qn
  D_Flip_Flop #(.trigger("falling")) d_ff_52 (
    .D(D[51]), .clk(Clock), .Q(Q[51]), .preset(1'b0), .reset(1'b0));  // open: Qn
  D_Flip_Flop #(.trigger("falling")) d_ff_53 (
    .D(D[52]), .clk(Clock), .Q(Q[52]), .preset(1'b0), .reset(1'b0));  // open: Qn
  D_Flip_Flop #(.trigger("falling")) d_ff_54 (
    .D(D[53]), .clk(Clock), .Q(Q[53]), .preset(1'b0), .reset(1'b0));  // open: Qn
  D_Flip_Flop #(.trigger("falling")) d_ff_55 (
    .D(D[54]), .clk(Clock), .Q(Q[54]), .preset(1'b0), .reset(1'b0));  // open: Qn
  D_Flip_Flop #(.trigger("falling")) d_ff_56 (
    .D(D[55]), .clk(Clock), .Q(Q[55]), .preset(1'b0), .reset(1'b0));  // open: Qn
  D_Flip_Flop #(.trigger("falling")) d_ff_57 (
    .D(D[56]), .clk(Clock), .Q(Q[56]), .preset(1'b0), .reset(1'b0));  // open: Qn
  D_Flip_Flop #(.trigger("falling")) d_ff_58 (
    .D(D[57]), .clk(Clock), .Q(Q[57]), .preset(1'b0), .reset(1'b0));  // open: Qn
  D_Flip_Flop #(.trigger("falling")) d_ff_59 (
    .D(D[58]), .clk(Clock), .Q(Q[58]), .preset(1'b0), .reset(1'b0));  // open: Qn
  D_Flip_Flop #(.trigger("falling")) d_ff_60 (
    .D(D[59]), .clk(Clock), .Q(Q[59]), .preset(1'b0), .reset(1'b0));  // open: Qn
  D_Flip_Flop #(.trigger("falling")) d_ff_61 (
    .D(D[60]), .clk(Clock), .Q(Q[60]), .preset(1'b0), .reset(1'b0));  // open: Qn
  D_Flip_Flop #(.trigger("falling")) d_ff_62 (
    .D(D[61]), .clk(Clock), .Q(Q[61]), .preset(1'b0), .reset(1'b0));  // open: Qn
  D_Flip_Flop #(.trigger("falling")) d_ff_63 (
    .D(D[62]), .clk(Clock), .Q(Q[62]), .preset(1'b0), .reset(1'b0));  // open: Qn
  D_Flip_Flop #(.trigger("falling")) d_ff_64 (
    .D(D[63]), .clk(Clock), .Q(Q[63]), .preset(1'b0), .reset(1'b0));  // open: Qn
endmodule

module PC_64 (
  input  Clock,
  input  PC_load,
  input  in_3,
  input  [31:0] I_low32,
  output [63:0] Q
);

  wire [63:0] adder_64_1_s, multiplexer_1_out, multiplexer_2_out;

  REG_64 reg_64_1 (.D(multiplexer_1_out), .Clock(Clock), .Q(Q));
  ADDER_64 adder_64_1 (.A(Q), .B({64{1'b0}}), .Cin(1'b1), .S(adder_64_1_s));  // open: S65
  Multiplexer #(.width(64)) multiplexer_1 (.in0(multiplexer_2_out), .in1(Q), .out(multiplexer_1_out), .sel(in_3));
  Multiplexer #(.width(64)) multiplexer_2 (
    .in0(adder_64_1_s), .in1({Q[63:32], I_low32}), .out(multiplexer_2_out), .sel(PC_load));
endmodule

module CU_64 (
  input  [31:0] IR_high32,
  output RegWrite,
  output MemRead,
  output OutEnable,
  output OP0,
  output OP1,
  output MemWrite,
  output PC_load,
  output LDA
);

  wire add, AN, RO, SUB;

  CU_LDA cu_lda_1 (.I(IR_high32), .LDA(LDA));
  CU_ADD cu_add_1 (.I(IR_high32), .ADD(add));
  CU_OUT cu_out_1 (.I(IR_high32), .OUT_64(OutEnable));
  CU_JMP cu_jmp_1 (.I(IR_high32), .JMP(PC_load));
  CU_STA cu_sta_1 (.I(IR_high32), .STA(MemWrite));
  CU_SUB cu_sub_1 (.I(IR_high32), .SUB(SUB));
  CU_AND cu_and_1 (.I(IR_high32), .AN(AN));
  CU_OR cu_or_1 (.I(IR_high32), .RO(RO));
  or or_1 (MemRead, LDA, SUB, AN, RO, add);
  or or_2 (OP0, SUB, RO);
  or or_3 (OP1, AN, RO);

  assign RegWrite = MemRead;

  // Other names for the same wires on the sheet: ir[31:0] = IR_high32; JMP = PC_load; out_64 = OutEnable;
  //   STA = MemWrite
endmodule

module CU_LDA (
  input  [31:0] I,
  output LDA
);

  wire [31:1] not_1_out;

  not not_1 (not_1_out[1], I[1]);
  not not_2 (not_1_out[2], I[2]);
  not not_3 (not_1_out[3], I[3]);
  not not_4 (not_1_out[4], I[4]);
  not not_5 (not_1_out[5], I[5]);
  not not_6 (not_1_out[6], I[6]);
  not not_7 (not_1_out[7], I[7]);
  not not_8 (not_1_out[8], I[8]);
  not not_9 (not_1_out[9], I[9]);
  not not_10 (not_1_out[10], I[10]);
  not not_11 (not_1_out[11], I[11]);
  not not_12 (not_1_out[12], I[12]);
  not not_13 (not_1_out[13], I[13]);
  not not_14 (not_1_out[14], I[14]);
  not not_15 (not_1_out[15], I[15]);
  not not_16 (not_1_out[16], I[16]);
  not not_17 (not_1_out[17], I[17]);
  not not_18 (not_1_out[18], I[18]);
  not not_19 (not_1_out[19], I[19]);
  not not_20 (not_1_out[20], I[20]);
  not not_21 (not_1_out[21], I[21]);
  not not_22 (not_1_out[22], I[22]);
  not not_23 (not_1_out[23], I[23]);
  not not_24 (not_1_out[24], I[24]);
  not not_25 (not_1_out[25], I[25]);
  not not_26 (not_1_out[26], I[26]);
  not not_27 (not_1_out[27], I[27]);
  not not_28 (not_1_out[28], I[28]);
  not not_29 (not_1_out[29], I[29]);
  not not_30 (not_1_out[30], I[30]);
  not not_31 (not_1_out[31], I[31]);
  and and_1 (LDA, I[0], not_1_out[1], not_1_out[2], not_1_out[3], not_1_out[4], not_1_out[5], not_1_out[6], not_1_out[7], not_1_out[8], not_1_out[9], not_1_out[10], not_1_out[11], not_1_out[12], not_1_out[13], not_1_out[14], not_1_out[15], not_1_out[16], not_1_out[17], not_1_out[18], not_1_out[19], not_1_out[20], not_1_out[21], not_1_out[22], not_1_out[23], not_1_out[24], not_1_out[25], not_1_out[26], not_1_out[27], not_1_out[28], not_1_out[29], not_1_out[30], not_1_out[31], 1'b1);
endmodule

module CU_ADD (
  input  [31:0] I,
  output ADD
);

  wire [31:1] not_1_out;

  not not_1 (not_1_out[1], I[1]);
  not not_2 (not_1_out[2], I[2]);
  not not_3 (not_1_out[3], I[3]);
  not not_4 (not_1_out[5], I[5]);
  not not_5 (not_1_out[6], I[6]);
  not not_6 (not_1_out[7], I[7]);
  not not_7 (not_1_out[8], I[8]);
  not not_8 (not_1_out[9], I[9]);
  not not_9 (not_1_out[10], I[10]);
  not not_10 (not_1_out[11], I[11]);
  not not_11 (not_1_out[12], I[12]);
  not not_12 (not_1_out[13], I[13]);
  not not_13 (not_1_out[14], I[14]);
  not not_14 (not_1_out[15], I[15]);
  not not_15 (not_1_out[16], I[16]);
  not not_16 (not_1_out[17], I[17]);
  not not_17 (not_1_out[18], I[18]);
  not not_18 (not_1_out[19], I[19]);
  not not_19 (not_1_out[20], I[20]);
  not not_20 (not_1_out[21], I[21]);
  not not_21 (not_1_out[22], I[22]);
  not not_22 (not_1_out[23], I[23]);
  not not_23 (not_1_out[24], I[24]);
  not not_24 (not_1_out[25], I[25]);
  not not_25 (not_1_out[26], I[26]);
  not not_26 (not_1_out[27], I[27]);
  not not_27 (not_1_out[28], I[28]);
  not not_28 (not_1_out[29], I[29]);
  not not_29 (not_1_out[30], I[30]);
  not not_30 (not_1_out[31], I[31]);
  and and_1 (ADD, I[0], not_1_out[1], not_1_out[2], not_1_out[3], I[4], not_1_out[5], not_1_out[6], not_1_out[7], not_1_out[8], not_1_out[9], not_1_out[10], not_1_out[11], not_1_out[12], not_1_out[13], not_1_out[14], not_1_out[15], not_1_out[16], not_1_out[17], not_1_out[18], not_1_out[19], not_1_out[20], not_1_out[21], not_1_out[22], not_1_out[23], not_1_out[24], not_1_out[25], not_1_out[26], not_1_out[27], not_1_out[28], not_1_out[29], not_1_out[30], not_1_out[31], 1'b1);
endmodule

module CU_OUT (
  input  [31:0] I,
  output OUT_64
);

  wire [31:0] not_1_out;

  not not_1 (not_1_out[0], I[0]);
  not not_2 (not_1_out[4], I[4]);
  not not_3 (not_1_out[5], I[5]);
  not not_4 (not_1_out[6], I[6]);
  not not_5 (not_1_out[7], I[7]);
  not not_6 (not_1_out[8], I[8]);
  not not_7 (not_1_out[9], I[9]);
  not not_8 (not_1_out[10], I[10]);
  not not_9 (not_1_out[11], I[11]);
  not not_10 (not_1_out[12], I[12]);
  not not_11 (not_1_out[13], I[13]);
  not not_12 (not_1_out[14], I[14]);
  not not_13 (not_1_out[15], I[15]);
  not not_14 (not_1_out[16], I[16]);
  not not_15 (not_1_out[17], I[17]);
  not not_16 (not_1_out[18], I[18]);
  not not_17 (not_1_out[19], I[19]);
  not not_18 (not_1_out[20], I[20]);
  not not_19 (not_1_out[21], I[21]);
  not not_20 (not_1_out[22], I[22]);
  not not_21 (not_1_out[23], I[23]);
  not not_22 (not_1_out[24], I[24]);
  not not_23 (not_1_out[25], I[25]);
  not not_24 (not_1_out[26], I[26]);
  not not_25 (not_1_out[27], I[27]);
  not not_26 (not_1_out[28], I[28]);
  not not_27 (not_1_out[29], I[29]);
  not not_28 (not_1_out[30], I[30]);
  not not_29 (not_1_out[31], I[31]);
  and and_1 (OUT_64, not_1_out[0], I[1], I[2], I[3], not_1_out[4], not_1_out[5], not_1_out[6], not_1_out[7], not_1_out[8], not_1_out[9], not_1_out[10], not_1_out[11], not_1_out[12], not_1_out[13], not_1_out[14], not_1_out[15], not_1_out[16], not_1_out[17], not_1_out[18], not_1_out[19], not_1_out[20], not_1_out[21], not_1_out[22], not_1_out[23], not_1_out[24], not_1_out[25], not_1_out[26], not_1_out[27], not_1_out[28], not_1_out[29], not_1_out[30], not_1_out[31], 1'b1);
endmodule

module CU_JMP (
  input  [31:0] I,
  output JMP
);

  wire [31:0] not_1_out;

  not not_1 (not_1_out[0], I[0]);
  not not_2 (not_1_out[1], I[1]);
  not not_3 (not_1_out[2], I[2]);
  not not_4 (not_1_out[4], I[4]);
  not not_5 (not_1_out[5], I[5]);
  not not_6 (not_1_out[6], I[6]);
  not not_7 (not_1_out[7], I[7]);
  not not_8 (not_1_out[8], I[8]);
  not not_9 (not_1_out[9], I[9]);
  not not_10 (not_1_out[10], I[10]);
  not not_11 (not_1_out[11], I[11]);
  not not_12 (not_1_out[12], I[12]);
  not not_13 (not_1_out[13], I[13]);
  not not_14 (not_1_out[14], I[14]);
  not not_15 (not_1_out[15], I[15]);
  not not_16 (not_1_out[16], I[16]);
  not not_17 (not_1_out[17], I[17]);
  not not_18 (not_1_out[18], I[18]);
  not not_19 (not_1_out[19], I[19]);
  not not_20 (not_1_out[20], I[20]);
  not not_21 (not_1_out[21], I[21]);
  not not_22 (not_1_out[22], I[22]);
  not not_23 (not_1_out[23], I[23]);
  not not_24 (not_1_out[24], I[24]);
  not not_25 (not_1_out[25], I[25]);
  not not_26 (not_1_out[26], I[26]);
  not not_27 (not_1_out[27], I[27]);
  not not_28 (not_1_out[28], I[28]);
  not not_29 (not_1_out[29], I[29]);
  not not_30 (not_1_out[30], I[30]);
  not not_31 (not_1_out[31], I[31]);
  and and_1 (JMP, not_1_out[0], not_1_out[1], not_1_out[2], I[3], not_1_out[4], not_1_out[5], not_1_out[6], not_1_out[7], not_1_out[8], not_1_out[9], not_1_out[10], not_1_out[11], not_1_out[12], not_1_out[13], not_1_out[14], not_1_out[15], not_1_out[16], not_1_out[17], not_1_out[18], not_1_out[19], not_1_out[20], not_1_out[21], not_1_out[22], not_1_out[23], not_1_out[24], not_1_out[25], not_1_out[26], not_1_out[27], not_1_out[28], not_1_out[29], not_1_out[30], not_1_out[31], 1'b1);
endmodule

module CPU_64 (
  input  [63:0] in_1,
  input  Clock,
  output [63:0] Read,
  output [63:0] CPU_out,
  output MemRead,
  output MemWrite,
  output [63:0] MemWrite_Data
);

  wire LDA, or_1_out, or_2_out, OutEnable, PC_load, RegWrite;
  wire [1:0] OP;
  wire [31:0] IR_high32, IR_low32;
  wire [63:0] ALU_B, pc_64_1_q, RD, REG_Q;

  or or_1 (or_1_out, RegWrite, MemWrite);
  PC_64 pc_64_1 (.Clock(Clock), .PC_load(PC_load), .in_3(or_1_out), .I_low32(IR_low32), .Q(pc_64_1_q));
  Multiplexer #(.width(64)) multiplexer_1 (.in0(pc_64_1_q), .in1({{32{1'b0}}, IR_low32}), .out(Read), .sel(or_2_out));
  or or_2 (or_2_out, MemRead, MemWrite);
  Multiplexer #(.width(64)) multiplexer_2 (.in0({64{1'b0}}), .in1(in_1), .out(ALU_B), .sel(RegWrite));
  IR_64 ir_64_1 (.D(in_1), .Clock(Clock), .Q({IR_high32, IR_low32}));
  CU_64 cu_64_1 (
    .IR_high32(IR_high32), .RegWrite(RegWrite), .MemRead(MemRead), .OutEnable(OutEnable), .OP0(OP[0]),
    .OP1(OP[1]), .MemWrite(MemWrite), .PC_load(PC_load), .LDA(LDA));
  assign MemWrite_Data = MemWrite ? REG_Q : 64'bz;  // Controlled_Buffer controlled_buffer_1
  assign CPU_out = OutEnable ? REG_Q : 64'bz;  // Controlled_Buffer controlled_buffer_2
  REG_64 reg_64_1 (.D(RD), .Clock(RegWrite), .Q(REG_Q));
  ALU_64 alu_64_1 (.A(REG_Q), .B(ALU_B), .OP(OP), .LDA(LDA), .R(RD));  // open: Borrow
endmodule

module CU_STA (
  input  [31:0] I,
  output STA
);

  wire [31:2] not_1_out;

  not not_1 (not_1_out[2], I[2]);
  not not_2 (not_1_out[3], I[3]);
  not not_3 (not_1_out[4], I[4]);
  not not_4 (not_1_out[5], I[5]);
  not not_5 (not_1_out[6], I[6]);
  not not_6 (not_1_out[7], I[7]);
  not not_7 (not_1_out[8], I[8]);
  not not_8 (not_1_out[9], I[9]);
  not not_9 (not_1_out[10], I[10]);
  not not_10 (not_1_out[11], I[11]);
  not not_11 (not_1_out[12], I[12]);
  not not_12 (not_1_out[13], I[13]);
  not not_13 (not_1_out[14], I[14]);
  not not_14 (not_1_out[15], I[15]);
  not not_15 (not_1_out[16], I[16]);
  not not_16 (not_1_out[17], I[17]);
  not not_17 (not_1_out[18], I[18]);
  not not_18 (not_1_out[19], I[19]);
  not not_19 (not_1_out[20], I[20]);
  not not_20 (not_1_out[21], I[21]);
  not not_21 (not_1_out[22], I[22]);
  not not_22 (not_1_out[23], I[23]);
  not not_23 (not_1_out[24], I[24]);
  not not_24 (not_1_out[25], I[25]);
  not not_25 (not_1_out[26], I[26]);
  not not_26 (not_1_out[27], I[27]);
  not not_27 (not_1_out[28], I[28]);
  not not_28 (not_1_out[29], I[29]);
  not not_29 (not_1_out[30], I[30]);
  not not_30 (not_1_out[31], I[31]);
  and and_1 (STA, I[0], I[1], not_1_out[2], not_1_out[3], not_1_out[4], not_1_out[5], not_1_out[6], not_1_out[7], not_1_out[8], not_1_out[9], not_1_out[10], not_1_out[11], not_1_out[12], not_1_out[13], not_1_out[14], not_1_out[15], not_1_out[16], not_1_out[17], not_1_out[18], not_1_out[19], not_1_out[20], not_1_out[21], not_1_out[22], not_1_out[23], not_1_out[24], not_1_out[25], not_1_out[26], not_1_out[27], not_1_out[28], not_1_out[29], not_1_out[30], not_1_out[31], 1'b1);
endmodule

module CU_SUB (
  input  [31:0] I,
  output SUB
);

  wire [31:0] not_1_out;

  not not_1 (not_1_out[0], I[0]);
  not not_2 (not_1_out[2], I[2]);
  not not_3 (not_1_out[3], I[3]);
  not not_4 (not_1_out[5], I[5]);
  not not_5 (not_1_out[6], I[6]);
  not not_6 (not_1_out[7], I[7]);
  not not_7 (not_1_out[8], I[8]);
  not not_8 (not_1_out[9], I[9]);
  not not_9 (not_1_out[10], I[10]);
  not not_10 (not_1_out[11], I[11]);
  not not_11 (not_1_out[12], I[12]);
  not not_12 (not_1_out[13], I[13]);
  not not_13 (not_1_out[14], I[14]);
  not not_14 (not_1_out[15], I[15]);
  not not_15 (not_1_out[16], I[16]);
  not not_16 (not_1_out[17], I[17]);
  not not_17 (not_1_out[18], I[18]);
  not not_18 (not_1_out[19], I[19]);
  not not_19 (not_1_out[20], I[20]);
  not not_20 (not_1_out[21], I[21]);
  not not_21 (not_1_out[22], I[22]);
  not not_22 (not_1_out[23], I[23]);
  not not_23 (not_1_out[24], I[24]);
  not not_24 (not_1_out[25], I[25]);
  not not_25 (not_1_out[26], I[26]);
  not not_26 (not_1_out[27], I[27]);
  not not_27 (not_1_out[28], I[28]);
  not not_28 (not_1_out[29], I[29]);
  not not_29 (not_1_out[30], I[30]);
  not not_30 (not_1_out[31], I[31]);
  and and_1 (SUB, not_1_out[0], I[1], not_1_out[2], not_1_out[3], I[4], not_1_out[5], not_1_out[6], not_1_out[7], not_1_out[8], not_1_out[9], not_1_out[10], not_1_out[11], not_1_out[12], not_1_out[13], not_1_out[14], not_1_out[15], not_1_out[16], not_1_out[17], not_1_out[18], not_1_out[19], not_1_out[20], not_1_out[21], not_1_out[22], not_1_out[23], not_1_out[24], not_1_out[25], not_1_out[26], not_1_out[27], not_1_out[28], not_1_out[29], not_1_out[30], not_1_out[31], 1'b1);
endmodule

module CU_AND (
  input  [31:0] I,
  output AN
);

  wire [31:2] not_1_out;

  not not_1 (not_1_out[2], I[2]);
  not not_2 (not_1_out[3], I[3]);
  not not_3 (not_1_out[5], I[5]);
  not not_4 (not_1_out[6], I[6]);
  not not_5 (not_1_out[7], I[7]);
  not not_6 (not_1_out[8], I[8]);
  not not_7 (not_1_out[9], I[9]);
  not not_8 (not_1_out[10], I[10]);
  not not_9 (not_1_out[11], I[11]);
  not not_10 (not_1_out[12], I[12]);
  not not_11 (not_1_out[13], I[13]);
  not not_12 (not_1_out[14], I[14]);
  not not_13 (not_1_out[15], I[15]);
  not not_14 (not_1_out[16], I[16]);
  not not_15 (not_1_out[17], I[17]);
  not not_16 (not_1_out[18], I[18]);
  not not_17 (not_1_out[19], I[19]);
  not not_18 (not_1_out[20], I[20]);
  not not_19 (not_1_out[21], I[21]);
  not not_20 (not_1_out[22], I[22]);
  not not_21 (not_1_out[23], I[23]);
  not not_22 (not_1_out[24], I[24]);
  not not_23 (not_1_out[25], I[25]);
  not not_24 (not_1_out[26], I[26]);
  not not_25 (not_1_out[27], I[27]);
  not not_26 (not_1_out[28], I[28]);
  not not_27 (not_1_out[29], I[29]);
  not not_28 (not_1_out[30], I[30]);
  not not_29 (not_1_out[31], I[31]);
  and and_1 (AN, I[0], I[1], not_1_out[2], not_1_out[3], I[4], not_1_out[5], not_1_out[6], not_1_out[7], not_1_out[8], not_1_out[9], not_1_out[10], not_1_out[11], not_1_out[12], not_1_out[13], not_1_out[14], not_1_out[15], not_1_out[16], not_1_out[17], not_1_out[18], not_1_out[19], not_1_out[20], not_1_out[21], not_1_out[22], not_1_out[23], not_1_out[24], not_1_out[25], not_1_out[26], not_1_out[27], not_1_out[28], not_1_out[29], not_1_out[30], not_1_out[31], 1'b1);
endmodule

module CU_OR (
  input  [31:0] I,
  output RO
);

  wire [31:0] not_1_out;

  not not_1 (not_1_out[0], I[0]);
  not not_2 (not_1_out[1], I[1]);
  not not_3 (not_1_out[3], I[3]);
  not not_4 (not_1_out[5], I[5]);
  not not_5 (not_1_out[6], I[6]);
  not not_6 (not_1_out[7], I[7]);
  not not_7 (not_1_out[8], I[8]);
  not not_8 (not_1_out[9], I[9]);
  not not_9 (not_1_out[10], I[10]);
  not not_10 (not_1_out[11], I[11]);
  not not_11 (not_1_out[12], I[12]);
  not not_12 (not_1_out[13], I[13]);
  not not_13 (not_1_out[14], I[14]);
  not not_14 (not_1_out[15], I[15]);
  not not_15 (not_1_out[16], I[16]);
  not not_16 (not_1_out[17], I[17]);
  not not_17 (not_1_out[18], I[18]);
  not not_18 (not_1_out[19], I[19]);
  not not_19 (not_1_out[20], I[20]);
  not not_20 (not_1_out[21], I[21]);
  not not_21 (not_1_out[22], I[22]);
  not not_22 (not_1_out[23], I[23]);
  not not_23 (not_1_out[24], I[24]);
  not not_24 (not_1_out[25], I[25]);
  not not_25 (not_1_out[26], I[26]);
  not not_26 (not_1_out[27], I[27]);
  not not_27 (not_1_out[28], I[28]);
  not not_28 (not_1_out[29], I[29]);
  not not_29 (not_1_out[30], I[30]);
  not not_30 (not_1_out[31], I[31]);
  and and_1 (RO, not_1_out[0], not_1_out[1], I[2], not_1_out[3], I[4], not_1_out[5], not_1_out[6], not_1_out[7], not_1_out[8], not_1_out[9], not_1_out[10], not_1_out[11], not_1_out[12], not_1_out[13], not_1_out[14], not_1_out[15], not_1_out[16], not_1_out[17], not_1_out[18], not_1_out[19], not_1_out[20], not_1_out[21], not_1_out[22], not_1_out[23], not_1_out[24], not_1_out[25], not_1_out[26], not_1_out[27], not_1_out[28], not_1_out[29], not_1_out[30], not_1_out[31], 1'b1);
endmodule
