// Logisim project sikir.circ as structural Verilog: 29 circuits, main circuit main
module main (
  output [63:0] out_1
);

  wire clk, MemRead, MemWrite, not_1_out;
  wire [23:0] cpu_64_1_read;
  wire [63:0] MemWrite_Data, ram_1_dout;
  wire [63:24] cpu_64_1_read_2;

  Clock clock_1 (.out(clk));
  not not_1 (not_1_out, MemWrite);
  RAM #(.addrWidth(24), .asyncread("true"), .dataWidth(64)) ram_1 (
    .addr(cpu_64_1_read), .we(MemWrite), .oe(not_1_out), .clk(clk), .din(MemWrite_Data), .dout(ram_1_dout));
  CPU_64 cpu_64_1 (
    .in_1(ram_1_dout), .Clock(clk), .Read({cpu_64_1_read_2, cpu_64_1_read}), .CPU_out(out_1),
    .MemRead(MemRead), .MemWrite(MemWrite), .MemWrite_Data(MemWrite_Data));
endmodule

module FA (
  input  A,
  input  B,
  input  Cin,
  output Sum,
  output Cout
);

  wire AND1_out, AND2_out, XOR1_out;

  xor XOR1 (XOR1_out, A, B);
  and AND1 (AND1_out, A, B);
  xor XOR2 (Sum, XOR1_out, Cin);
  and AND2 (AND2_out, XOR1_out, Cin);
  or or_1 (Cout, AND1_out, AND2_out);
endmodule

module ADDER_64 (
  input  [63:0] A,
  input  [63:0] B,
  input  Cin,
  output [63:0] S,
  output S64,
  output ADDER_OF
);

  wire [62:0] CC;

  FA fa_1 (.A(A[0]), .B(B[0]), .Cin(Cin), .Sum(S[0]), .Cout(CC[0]));
  FA fa_2 (.A(A[1]), .B(B[1]), .Cin(CC[0]), .Sum(S[1]), .Cout(CC[1]));
  FA fa_3 (.A(A[2]), .B(B[2]), .Cin(CC[1]), .Sum(S[2]), .Cout(CC[2]));
  FA fa_4 (.A(A[3]), .B(B[3]), .Cin(CC[2]), .Sum(S[3]), .Cout(CC[3]));
  FA fa_5 (.A(A[4]), .B(B[4]), .Cin(CC[3]), .Sum(S[4]), .Cout(CC[4]));
  FA fa_6 (.A(A[5]), .B(B[5]), .Cin(CC[4]), .Sum(S[5]), .Cout(CC[5]));
  FA fa_7 (.A(A[6]), .B(B[6]), .Cin(CC[5]), .Sum(S[6]), .Cout(CC[6]));
  FA fa_8 (.A(A[7]), .B(B[7]), .Cin(CC[6]), .Sum(S[7]), .Cout(CC[7]));
  FA fa_9 (.A(A[8]), .B(B[8]), .Cin(CC[7]), .Sum(S[8]), .Cout(CC[8]));
  FA fa_10 (.A(A[9]), .B(B[9]), .Cin(CC[8]), .Sum(S[9]), .Cout(CC[9]));
  FA fa_11 (.A(A[10]), .B(B[10]), .Cin(CC[9]), .Sum(S[10]), .Cout(CC[10]));
  FA fa_12 (.A(A[11]), .B(B[11]), .Cin(CC[10]), .Sum(S[11]), .Cout(CC[11]));
  FA fa_13 (.A(A[12]), .B(B[12]), .Cin(CC[11]), .Sum(S[12]), .Cout(CC[12]));
  FA fa_14 (.A(A[13]), .B(B[13]), .Cin(CC[12]), .Sum(S[13]), .Cout(CC[13]));
  FA fa_15 (.A(A[14]), .B(B[14]), .Cin(CC[13]), .Sum(S[14]), .Cout(CC[14]));
  FA fa_16 (.A(A[15]), .B(B[15]), .Cin(CC[14]), .Sum(S[15]), .Cout(CC[15]));
  FA fa_17 (.A(A[16]), .B(B[16]), .Cin(CC[15]), .Sum(S[16]), .Cout(CC[16]));
  FA fa_18 (.A(A[17]), .B(B[17]), .Cin(CC[16]), .Sum(S[17]), .Cout(CC[17]));
  FA fa_19 (.A(A[18]), .B(B[18]), .Cin(CC[17]), .Sum(S[18]), .Cout(CC[18]));
  FA fa_20 (.A(A[19]), .B(B[19]), .Cin(CC[18]), .Sum(S[19]), .Cout(CC[19]));
  FA fa_21 (.A(A[20]), .B(B[20]), .Cin(CC[19]), .Sum(S[20]), .Cout(CC[20]));
  FA fa_22 (.A(A[21]), .B(B[21]), .Cin(CC[20]), .Sum(S[21]), .Cout(CC[21]));
  FA fa_23 (.A(A[22]), .B(B[22]), .Cin(CC[21]), .Sum(S[22]), .Cout(CC[22]));
  FA fa_24 (.A(A[23]), .B(B[23]), .Cin(CC[22]), .Sum(S[23]), .Cout(CC[23]));
  FA fa_25 (.A(A[24]), .B(B[24]), .Cin(CC[23]), .Sum(S[24]), .Cout(CC[24]));
  FA fa_26 (.A(A[25]), .B(B[25]), .Cin(CC[24]), .Sum(S[25]), .Cout(CC[25]));
  FA fa_27 (.A(A[26]), .B(B[26]), .Cin(CC[25]), .Sum(S[26]), .Cout(CC[26]));
  FA fa_28 (.A(A[27]), .B(B[27]), .Cin(CC[26]), .Sum(S[27]), .Cout(CC[27]));
  FA fa_29 (.A(A[28]), .B(B[28]), .Cin(CC[27]), .Sum(S[28]), .Cout(CC[28]));
  FA fa_30 (.A(A[29]), .B(B[29]), .Cin(CC[28]), .Sum(S[29]), .Cout(CC[29]));
  FA fa_31 (.A(A[30]), .B(B[30]), .Cin(CC[29]), .Sum(S[30]), .Cout(CC[30]));
  FA fa_32 (.A(A[31]), .B(B[31]), .Cin(CC[30]), .Sum(S[31]), .Cout(CC[31]));
  FA fa_33 (.A(A[32]), .B(B[32]), .Cin(CC[31]), .Sum(S[32]), .Cout(CC[32]));
  FA fa_34 (.A(A[33]), .B(B[33]), .Cin(CC[32]), .Sum(S[33]), .Cout(CC[33]));
  FA fa_35 (.A(A[34]), .B(B[34]), .Cin(CC[33]), .Sum(S[34]), .Cout(CC[34]));
  FA fa_36 (.A(A[35]), .B(B[35]), .Cin(CC[34]), .Sum(S[35]), .Cout(CC[35]));
  FA fa_37 (.A(A[36]), .B(B[36]), .Cin(CC[35]), .Sum(S[36]), .Cout(CC[36]));
  FA fa_38 (.A(A[37]), .B(B[37]), .Cin(CC[36]), .Sum(S[37]), .Cout(CC[37]));
  FA fa_39 (.A(A[38]), .B(B[38]), .Cin(CC[37]), .Sum(S[38]), .Cout(CC[38]));
  FA fa_40 (.A(A[39]), .B(B[39]), .Cin(CC[38]), .Sum(S[39]), .Cout(CC[39]));
  FA fa_41 (.A(A[40]), .B(B[40]), .Cin(CC[39]), .Sum(S[40]), .Cout(CC[40]));
  FA fa_42 (.A(A[41]), .B(B[41]), .Cin(CC[40]), .Sum(S[41]), .Cout(CC[41]));
  FA fa_43 (.A(A[42]), .B(B[42]), .Cin(CC[41]), .Sum(S[42]), .Cout(CC[42]));
  FA fa_44 (.A(A[43]), .B(B[43]), .Cin(CC[42]), .Sum(S[43]), .Cout(CC[43]));
  FA fa_45 (.A(A[44]), .B(B[44]), .Cin(CC[43]), .Sum(S[44]), .Cout(CC[44]));
  FA fa_46 (.A(A[45]), .B(B[45]), .Cin(CC[44]), .Sum(S[45]), .Cout(CC[45]));
  FA fa_47 (.A(A[46]), .B(B[46]), .Cin(CC[45]), .Sum(S[46]), .Cout(CC[46]));
  FA fa_48 (.A(A[47]), .B(B[47]), .Cin(CC[46]), .Sum(S[47]), .Cout(CC[47]));
  FA fa_49 (.A(A[48]), .B(B[48]), .Cin(CC[47]), .Sum(S[48]), .Cout(CC[48]));
  FA fa_50 (.A(A[49]), .B(B[49]), .Cin(CC[48]), .Sum(S[49]), .Cout(CC[49]));
  FA fa_51 (.A(A[50]), .B(B[50]), .Cin(CC[49]), .Sum(S[50]), .Cout(CC[50]));
  FA fa_52 (.A(A[51]), .B(B[51]), .Cin(CC[50]), .Sum(S[51]), .Cout(CC[51]));
  FA fa_53 (.A(A[52]), .B(B[52]), .Cin(CC[51]), .Sum(S[52]), .Cout(CC[52]));
  FA fa_54 (.A(A[53]), .B(B[53]), .Cin(CC[52]), .Sum(S[53]), .Cout(CC[53]));
  FA fa_55 (.A(A[54]), .B(B[54]), .Cin(CC[53]), .Sum(S[54]), .Cout(CC[54]));
  FA fa_56 (.A(A[55]), .B(B[55]), .Cin(CC[54]), .Sum(S[55]), .Cout(CC[55]));
  FA fa_57 (.A(A[56]), .B(B[56]), .Cin(CC[55]), .Sum(S[56]), .Cout(CC[56]));
  FA fa_58 (.A(A[57]), .B(B[57]), .Cin(CC[56]), .Sum(S[57]), .Cout(CC[57]));
  FA fa_59 (.A(A[58]), .B(B[58]), .Cin(CC[57]), .Sum(S[58]), .Cout(CC[58]));
  FA fa_60 (.A(A[59]), .B(B[59]), .Cin(CC[58]), .Sum(S[59]), .Cout(CC[59]));
  FA fa_61 (.A(A[60]), .B(B[60]), .Cin(CC[59]), .Sum(S[60]), .Cout(CC[60]));
  FA fa_62 (.A(A[61]), .B(B[61]), .Cin(CC[60]), .Sum(S[61]), .Cout(CC[61]));
  FA fa_63 (.A(A[62]), .B(B[62]), .Cin(CC[61]), .Sum(S[62]), .Cout(CC[62]));
  FA fa_64 (.A(A[63]), .B(B[63]), .Cin(CC[62]), .Sum(S[63]), .Cout(S64));
  xor xor_1 (ADDER_OF, S[63], S64);
endmodule

module SUBTRACTOR_64 (
  input  [63:0] A,
  input  [63:0] B,
  output [63:0] diff,
  output Borrow,
  output SUB_OF
);

  wire adder_64_1_adder_of, adder_64_1_s64;
  wire [63:0] not_1_out;

  assign not_1_out = ~B;  // NOT_Gate not_1, 64 bits wide
  ADDER_64 adder_64_1 (
    .A(A), .B(not_1_out), .Cin(1'b1), .S(diff), .S64(adder_64_1_s64), .ADDER_OF(adder_64_1_adder_of));
  not not_2 (Borrow, adder_64_1_s64);
  not not_3 (SUB_OF, adder_64_1_adder_of);
endmodule

module AND_64 (
  input  [63:0] in_1,
  input  [63:0] in_2,
  output [63:0] out_3
);

  and and_1 (out_3[0], in_1[0], in_2[0]);
  and and_2 (out_3[1], in_1[1], in_2[1]);
  and and_3 (out_3[2], in_1[2], in_2[2]);
  and and_4 (out_3[3], in_1[3], in_2[3]);
  and and_5 (out_3[4], in_1[4], in_2[4]);
  and and_6 (out_3[5], in_1[5], in_2[5]);
  and and_7 (out_3[6], in_1[6], in_2[6]);
  and and_8 (out_3[7], in_1[7], in_2[7]);
  and and_9 (out_3[8], in_1[8], in_2[8]);
  and and_10 (out_3[9], in_1[9], in_2[9]);
  and and_11 (out_3[10], in_1[10], in_2[10]);
  and and_12 (out_3[11], in_1[11], in_2[11]);
  and and_13 (out_3[12], in_1[12], in_2[12]);
  and and_14 (out_3[13], in_1[13], in_2[13]);
  and and_15 (out_3[14], in_1[14], in_2[14]);
  and and_16 (out_3[15], in_1[15], in_2[15]);
  and and_17 (out_3[16], in_1[16], in_2[16]);
  and and_18 (out_3[17], in_1[17], in_2[17]);
  and and_19 (out_3[18], in_1[18], in_2[18]);
  and and_20 (out_3[19], in_1[19], in_2[19]);
  and and_21 (out_3[20], in_1[20], in_2[20]);
  and and_22 (out_3[21], in_1[21], in_2[21]);
  and and_23 (out_3[22], in_1[22], in_2[22]);
  and and_24 (out_3[23], in_1[23], in_2[23]);
  and and_25 (out_3[24], in_1[24], in_2[24]);
  and and_26 (out_3[25], in_1[25], in_2[25]);
  and and_27 (out_3[26], in_1[26], in_2[26]);
  and and_28 (out_3[27], in_1[27], in_2[27]);
  and and_29 (out_3[28], in_1[28], in_2[28]);
  and and_30 (out_3[29], in_1[29], in_2[29]);
  and and_31 (out_3[30], in_1[30], in_2[30]);
  and and_32 (out_3[31], in_1[31], in_2[31]);
  and and_33 (out_3[32], in_1[32], in_2[32]);
  and and_34 (out_3[33], in_1[33], in_2[33]);
  and and_35 (out_3[34], in_1[34], in_2[34]);
  and and_36 (out_3[35], in_1[35], in_2[35]);
  and and_37 (out_3[36], in_1[36], in_2[36]);
  and and_38 (out_3[37], in_1[37], in_2[37]);
  and and_39 (out_3[38], in_1[38], in_2[38]);
  and and_40 (out_3[39], in_1[39], in_2[39]);
  and and_41 (out_3[40], in_1[40], in_2[40]);
  and and_42 (out_3[41], in_1[41], in_2[41]);
  and and_43 (out_3[42], in_1[42], in_2[42]);
  and and_44 (out_3[43], in_1[43], in_2[43]);
  and and_45 (out_3[44], in_1[44], in_2[44]);
  and and_46 (out_3[45], in_1[45], in_2[45]);
  and and_47 (out_3[46], in_1[46], in_2[46]);
  and and_48 (out_3[47], in_1[47], in_2[47]);
  and and_49 (out_3[48], in_1[48], in_2[48]);
  and and_50 (out_3[49], in_1[49], in_2[49]);
  and and_51 (out_3[50], in_1[50], in_2[50]);
  and and_52 (out_3[51], in_1[51], in_2[51]);
  and and_53 (out_3[52], in_1[52], in_2[52]);
  and and_54 (out_3[53], in_1[53], in_2[53]);
  and and_55 (out_3[54], in_1[54], in_2[54]);
  and and_56 (out_3[55], in_1[55], in_2[55]);
  and and_57 (out_3[56], in_1[56], in_2[56]);
  and and_58 (out_3[57], in_1[57], in_2[57]);
  and and_59 (out_3[58], in_1[58], in_2[58]);
  and and_60 (out_3[59], in_1[59], in_2[59]);
  and and_61 (out_3[60], in_1[60], in_2[60]);
  and and_62 (out_3[61], in_1[61], in_2[61]);
  and and_63 (out_3[62], in_1[62], in_2[62]);
  and and_64 (out_3[63], in_1[63], in_2[63]);
endmodule

module OR_64 (
  input  [63:0] in_1,
  input  [63:0] in_2,
  output [63:0] out_3
);

  or or_1 (out_3[0], in_1[0], in_2[0]);
  or or_2 (out_3[1], in_1[1], in_2[1]);
  or or_3 (out_3[2], in_1[2], in_2[2]);
  or or_4 (out_3[3], in_1[3], in_2[3]);
  or or_5 (out_3[4], in_1[4], in_2[4]);
  or or_6 (out_3[5], in_1[5], in_2[5]);
  or or_7 (out_3[6], in_1[6], in_2[6]);
  or or_8 (out_3[7], in_1[7], in_2[7]);
  or or_9 (out_3[8], in_1[8], in_2[8]);
  or or_10 (out_3[9], in_1[9], in_2[9]);
  or or_11 (out_3[10], in_1[10], in_2[10]);
  or or_12 (out_3[11], in_1[11], in_2[11]);
  or or_13 (out_3[12], in_1[12], in_2[12]);
  or or_14 (out_3[13], in_1[13], in_2[13]);
  or or_15 (out_3[14], in_1[14], in_2[14]);
  or or_16 (out_3[15], in_1[15], in_2[15]);
  or or_17 (out_3[16], in_1[16], in_2[16]);
  or or_18 (out_3[17], in_1[17], in_2[17]);
  or or_19 (out_3[18], in_1[18], in_2[18]);
  or or_20 (out_3[19], in_1[19], in_2[19]);
  or or_21 (out_3[20], in_1[20], in_2[20]);
  or or_22 (out_3[21], in_1[21], in_2[21]);
  or or_23 (out_3[22], in_1[22], in_2[22]);
  or or_24 (out_3[23], in_1[23], in_2[23]);
  or or_25 (out_3[24], in_1[24], in_2[24]);
  or or_26 (out_3[25], in_1[25], in_2[25]);
  or or_27 (out_3[26], in_1[26], in_2[26]);
  or or_28 (out_3[27], in_1[27], in_2[27]);
  or or_29 (out_3[28], in_1[28], in_2[28]);
  or or_30 (out_3[29], in_1[29], in_2[29]);
  or or_31 (out_3[30], in_1[30], in_2[30]);
  or or_32 (out_3[31], in_1[31], in_2[31]);
  or or_33 (out_3[32], in_1[32], in_2[32]);
  or or_34 (out_3[33], in_1[33], in_2[33]);
  or or_35 (out_3[34], in_1[34], in_2[34]);
  or or_36 (out_3[35], in_1[35], in_2[35]);
  or or_37 (out_3[36], in_1[36], in_2[36]);
  or or_38 (out_3[37], in_1[37], in_2[37]);
  or or_39 (out_3[38], in_1[38], in_2[38]);
  or or_40 (out_3[39], in_1[39], in_2[39]);
  or or_41 (out_3[40], in_1[40], in_2[40]);
  or or_42 (out_3[41], in_1[41], in_2[41]);
  or or_43 (out_3[42], in_1[42], in_2[42]);
  or or_44 (out_3[43], in_1[43], in_2[43]);
  or or_45 (out_3[44], in_1[44], in_2[44]);
  or or_46 (out_3[45], in_1[45], in_2[45]);
  or or_47 (out_3[46], in_1[46], in_2[46]);
  or or_48 (out_3[47], in_1[47], in_2[47]);
  or or_49 (out_3[48], in_1[48], in_2[48]);
  or or_50 (out_3[49], in_1[49], in_2[49]);
  or or_51 (out_3[50], in_1[50], in_2[50]);
  or or_52 (out_3[51], in_1[51], in_2[51]);
  or or_53 (out_3[52], in_1[52], in_2[52]);
  or or_54 (out_3[53], in_1[53], in_2[53]);
  or or_55 (out_3[54], in_1[54], in_2[54]);
  or or_56 (out_3[55], in_1[55], in_2[55]);
  or or_57 (out_3[56], in_1[56], in_2[56]);
  or or_58 (out_3[57], in_1[57], in_2[57]);
  or or_59 (out_3[58], in_1[58], in_2[58]);
  or or_60 (out_3[59], in_1[59], in_2[59]);
  or or_61 (out_3[60], in_1[60], in_2[60]);
  or or_62 (out_3[61], in_1[61], in_2[61]);
  or or_63 (out_3[62], in_1[62], in_2[62]);
  or or_64 (out_3[63], in_1[63], in_2[63]);
endmodule

module ALU_64 (
  input  [63:0] A,
  input  [63:0] B,
  input  [1:0] OP,
  input  [63:0] LDA_data,
  input  LDA,
  output [63:0] R,
  output CF,
  output ALU_OF,
  output ZF,
  output SF
);

  wire adder_64_1_adder_of, adder_64_1_s64, subtractor_64_1_borrow, subtractor_64_1_sub_of;
  wire [62:0] multiplexer_2_out;
  wire [63:0] AN, DIFF, RO, S;

  ADDER_64 adder_64_1 (.A(A), .B(B), .Cin(1'b0), .S(S), .S64(adder_64_1_s64), .ADDER_OF(adder_64_1_adder_of));
  SUBTRACTOR_64 subtractor_64_1 (
    .A(A), .B(B), .diff(DIFF), .Borrow(subtractor_64_1_borrow), .SUB_OF(subtractor_64_1_sub_of));
  AND_64 and_64_1 (.in_1(A), .in_2(B), .out_3(AN));
  OR_64 or_64_1 (.in_1(A), .in_2(B), .out_3(RO));
  Multiplexer #(.width(64)) multiplexer_1 (
    .in0({SF, multiplexer_2_out[62:33], SF, multiplexer_2_out[31:0]}), .in1(LDA_data), .out(R), .sel(LDA));
  Multiplexer #(.select(2), .width(64)) multiplexer_2 (
    .in0(S), .in1(DIFF), .in2(AN), .in3(RO),
    .out({SF, multiplexer_2_out[62:33], SF, multiplexer_2_out[31:0]}), .sel(OP));
  Multiplexer #(.select(2)) multiplexer_3 (
    .in0(adder_64_1_s64), .in1(subtractor_64_1_borrow), .in2(1'b0), .in3(1'b0), .out(CF), .sel(OP));
  Multiplexer #(.select(2)) multiplexer_4 (
    .in0(adder_64_1_adder_of), .in1(subtractor_64_1_sub_of), .in2(1'b0), .in3(1'b0), .out(ALU_OF), .sel(OP));
  nor nor_1 (ZF, multiplexer_2_out[0], multiplexer_2_out[1], multiplexer_2_out[2], multiplexer_2_out[3], multiplexer_2_out[4], multiplexer_2_out[5], multiplexer_2_out[6], multiplexer_2_out[7], multiplexer_2_out[8], multiplexer_2_out[9], multiplexer_2_out[10], multiplexer_2_out[11], multiplexer_2_out[12], multiplexer_2_out[13], multiplexer_2_out[14], multiplexer_2_out[15], multiplexer_2_out[16], multiplexer_2_out[17], multiplexer_2_out[18], multiplexer_2_out[19], multiplexer_2_out[20], multiplexer_2_out[21], multiplexer_2_out[22], multiplexer_2_out[23], multiplexer_2_out[24], multiplexer_2_out[25], multiplexer_2_out[26], multiplexer_2_out[27], multiplexer_2_out[28], multiplexer_2_out[29], multiplexer_2_out[30], multiplexer_2_out[31], multiplexer_2_out[33], multiplexer_2_out[34], multiplexer_2_out[35], multiplexer_2_out[36], multiplexer_2_out[37], multiplexer_2_out[38], multiplexer_2_out[39], multiplexer_2_out[40], multiplexer_2_out[41], multiplexer_2_out[42], multiplexer_2_out[43], multiplexer_2_out[44], multiplexer_2_out[45], multiplexer_2_out[46], multiplexer_2_out[47], multiplexer_2_out[48], multiplexer_2_out[49], multiplexer_2_out[50], multiplexer_2_out[51], multiplexer_2_out[52], multiplexer_2_out[53], multiplexer_2_out[54], multiplexer_2_out[55], multiplexer_2_out[56], multiplexer_2_out[57], multiplexer_2_out[58], multiplexer_2_out[59], multiplexer_2_out[60], multiplexer_2_out[61], multiplexer_2_out[62], SF, SF);
endmodule

module IR_64 (
  input  [63:0] D,
  input  Clock,
  output [63:0] Q
);

  D_Flip_Flop d_ff_1 (.D(D[0]), .clk(Clock), .Q(Q[0]), .preset(1'b0), .reset(1'b0));  // open: Qn
  D_Flip_Flop d_ff_2 (.D(D[1]), .clk(Clock), .Q(Q[1]), .reset(1'b0));  // open: Qn, preset
  D_Flip_Flop d_ff_3 (.D(D[2]), .clk(Clock), .Q(Q[2]), .reset(1'b0));  // open: Qn, preset
  D_Flip_Flop d_ff_4 (.D(D[3]), .clk(Clock), .Q(Q[3]), .reset(1'b0));  // open: Qn, preset
  D_Flip_Flop d_ff_5 (.D(D[4]), .clk(Clock), .Q(Q[4]), .reset(1'b0));  // open: Qn, preset
  D_Flip_Flop d_ff_6 (.D(D[5]), .clk(Clock), .Q(Q[5]), .reset(1'b0));  // open: Qn, preset
  D_Flip_Flop d_ff_7 (.D(D[6]), .clk(Clock), .Q(Q[6]), .reset(1'b0));  // open: Qn, preset
  D_Flip_Flop d_ff_8 (.D(D[7]), .clk(Clock), .Q(Q[7]), .reset(1'b0));  // open: Qn, preset
  D_Flip_Flop d_ff_9 (.D(D[8]), .clk(Clock), .Q(Q[8]), .reset(1'b0));  // open: Qn, preset
  D_Flip_Flop d_ff_10 (.D(D[9]), .clk(Clock), .Q(Q[9]), .reset(1'b0));  // open: Qn, preset
  D_Flip_Flop d_ff_11 (.D(D[10]), .clk(Clock), .Q(Q[10]), .reset(1'b0));  // open: Qn, preset
  D_Flip_Flop d_ff_12 (.D(D[11]), .clk(Clock), .Q(Q[11]), .reset(1'b0));  // open: Qn, preset
  D_Flip_Flop d_ff_13 (.D(D[12]), .clk(Clock), .Q(Q[12]), .reset(1'b0));  // open: Qn, preset
  D_Flip_Flop d_ff_14 (.D(D[13]), .clk(Clock), .Q(Q[13]), .reset(1'b0));  // open: Qn, preset
  D_Flip_Flop d_ff_15 (.D(D[14]), .clk(Clock), .Q(Q[14]), .reset(1'b0));  // open: Qn, preset
  D_Flip_Flop d_ff_16 (.D(D[15]), .clk(Clock), .Q(Q[15]), .reset(1'b0));  // open: Qn, preset
  D_Flip_Flop d_ff_17 (.D(D[16]), .clk(Clock), .Q(Q[16]), .reset(1'b0));  // open: Qn, preset
  D_Flip_Flop d_ff_18 (.D(D[17]), .clk(Clock), .Q(Q[17]), .reset(1'b0));  // open: Qn, preset
  D_Flip_Flop d_ff_19 (.D(D[18]), .clk(Clock), .Q(Q[18]), .reset(1'b0));  // open: Qn, preset
  D_Flip_Flop d_ff_20 (.D(D[19]), .clk(Clock), .Q(Q[19]), .reset(1'b0));  // open: Qn, preset
  D_Flip_Flop d_ff_21 (.D(D[20]), .clk(Clock), .Q(Q[20]), .reset(1'b0));  // open: Qn, preset
  D_Flip_Flop d_ff_22 (.D(D[21]), .clk(Clock), .Q(Q[21]), .reset(1'b0));  // open: Qn, preset
  D_Flip_Flop d_ff_23 (.D(D[22]), .clk(Clock), .Q(Q[22]), .reset(1'b0));  // open: Qn, preset
  D_Flip_Flop d_ff_24 (.D(D[23]), .clk(Clock), .Q(Q[23]), .reset(1'b0));  // open: Qn, preset
  D_Flip_Flop d_ff_25 (.D(D[24]), .clk(Clock), .Q(Q[24]), .reset(1'b0));  // open: Qn, preset
  D_Flip_Flop d_ff_26 (.D(D[25]), .clk(Clock), .Q(Q[25]), .reset(1'b0));  // open: Qn, preset
  D_Flip_Flop d_ff_27 (.D(D[26]), .clk(Clock), .Q(Q[26]), .reset(1'b0));  // open: Qn, preset
  D_Flip_Flop d_ff_28 (.D(D[27]), .clk(Clock), .Q(Q[27]), .reset(1'b0));  // open: Qn, preset
  D_Flip_Flop d_ff_29 (.D(D[28]), .clk(Clock), .Q(Q[28]), .reset(1'b0));  // open: Qn, preset
  D_Flip_Flop d_ff_30 (.D(D[29]), .clk(Clock), .Q(Q[29]), .reset(1'b0));  // open: Qn, preset
  D_Flip_Flop d_ff_31 (.D(D[30]), .clk(Clock), .Q(Q[30]), .reset(1'b0));  // open: Qn, preset
  D_Flip_Flop d_ff_32 (.D(D[31]), .clk(Clock), .Q(Q[31]), .reset(1'b0));  // open: Qn, preset
  D_Flip_Flop d_ff_33 (.D(D[32]), .clk(Clock), .Q(Q[32]), .reset(1'b0));  // open: Qn, preset
  D_Flip_Flop d_ff_34 (.D(D[33]), .clk(Clock), .Q(Q[33]), .reset(1'b0));  // open: Qn, preset
  D_Flip_Flop d_ff_35 (.D(D[34]), .clk(Clock), .Q(Q[34]), .reset(1'b0));  // open: Qn, preset
  D_Flip_Flop d_ff_36 (.D(D[35]), .clk(Clock), .Q(Q[35]), .reset(1'b0));  // open: Qn, preset
  D_Flip_Flop d_ff_37 (.D(D[36]), .clk(Clock), .Q(Q[36]), .reset(1'b0));  // open: Qn, preset
  D_Flip_Flop d_ff_38 (.D(D[37]), .clk(Clock), .Q(Q[37]), .reset(1'b0));  // open: Qn, preset
  D_Flip_Flop d_ff_39 (.D(D[38]), .clk(Clock), .Q(Q[38]), .reset(1'b0));  // open: Qn, preset
  D_Flip_Flop d_ff_40 (.D(D[39]), .clk(Clock), .Q(Q[39]), .reset(1'b0));  // open: Qn, preset
  D_Flip_Flop d_ff_41 (.D(D[40]), .clk(Clock), .Q(Q[40]), .reset(1'b0));  // open: Qn, preset
  D_Flip_Flop d_ff_42 (.D(D[41]), .clk(Clock), .Q(Q[41]), .reset(1'b0));  // open: Qn, preset
  D_Flip_Flop d_ff_43 (.D(D[42]), .clk(Clock), .Q(Q[42]), .reset(1'b0));  // open: Qn, preset
  D_Flip_Flop d_ff_44 (.D(D[43]), .clk(Clock), .Q(Q[43]), .reset(1'b0));  // open: Qn, preset
  D_Flip_Flop d_ff_45 (.D(D[44]), .clk(Clock), .Q(Q[44]), .reset(1'b0));  // open: Qn, preset
  D_Flip_Flop d_ff_46 (.D(D[45]), .clk(Clock), .Q(Q[45]), .reset(1'b0));  // open: Qn, preset
  D_Flip_Flop d_ff_47 (.D(D[46]), .clk(Clock), .Q(Q[46]), .reset(1'b0));  // open: Qn, preset
  D_Flip_Flop d_ff_48 (.D(D[47]), .clk(Clock), .Q(Q[47]), .reset(1'b0));  // open: Qn, preset
  D_Flip_Flop d_ff_49 (.D(D[48]), .clk(Clock), .Q(Q[48]), .reset(1'b0));  // open: Qn, preset
  D_Flip_Flop d_ff_50 (.D(D[49]), .clk(Clock), .Q(Q[49]), .reset(1'b0));  // open: Qn, preset
  D_Flip_Flop d_ff_51 (.D(D[50]), .clk(Clock), .Q(Q[50]), .reset(1'b0));  // open: Qn, preset
  D_Flip_Flop d_ff_52 (.D(D[51]), .clk(Clock), .Q(Q[51]), .reset(1'b0));  // open: Qn, preset
  D_Flip_Flop d_ff_53 (.D(D[52]), .clk(Clock), .Q(Q[52]), .reset(1'b0));  // open: Qn, preset
  D_Flip_Flop d_ff_54 (.D(D[53]), .clk(Clock), .Q(Q[53]), .reset(1'b0));  // open: Qn, preset
  D_Flip_Flop d_ff_55 (.D(D[54]), .clk(Clock), .Q(Q[54]), .reset(1'b0));  // open: Qn, preset
  D_Flip_Flop d_ff_56 (.D(D[55]), .clk(Clock), .Q(Q[55]), .reset(1'b0));  // open: Qn, preset
  D_Flip_Flop d_ff_57 (.D(D[56]), .clk(Clock), .Q(Q[56]), .reset(1'b0));  // open: Qn, preset
  D_Flip_Flop d_ff_58 (.D(D[57]), .clk(Clock), .Q(Q[57]), .reset(1'b0));  // open: Qn, preset
  D_Flip_Flop d_ff_59 (.D(D[58]), .clk(Clock), .Q(Q[58]), .reset(1'b0));  // open: Qn, preset
  D_Flip_Flop d_ff_60 (.D(D[59]), .clk(Clock), .Q(Q[59]), .reset(1'b0));  // open: Qn, preset
  D_Flip_Flop d_ff_61 (.D(D[60]), .clk(Clock), .Q(Q[60]), .reset(1'b0));  // open: Qn, preset
  D_Flip_Flop d_ff_62 (.D(D[61]), .clk(Clock), .Q(Q[61]), .reset(1'b0));  // open: Qn, preset
  D_Flip_Flop d_ff_63 (.D(D[62]), .clk(Clock), .Q(Q[62]), .reset(1'b0));  // open: Qn, preset
  D_Flip_Flop d_ff_64 (.D(D[63]), .clk(Clock), .Q(Q[63]));  // open: Qn, preset, reset
endmodule

module PC_64 (
  input  Clock,
  input  PC_load,
  input  in_3,
  input  [31:0] I_low32,
  output [63:0] Q
);

  wire [63:0] adder_64_1_s, multiplexer_1_out, multiplexer_2_out;

  Register #(.width(64)) register_1 (.D(multiplexer_1_out), .en(1'b1), .clk(Clock), .Q(Q));  // open: clr
  ADDER_64 adder_64_1 (.A(Q), .B({64{1'b0}}), .Cin(1'b1), .S(adder_64_1_s));  // open: S64, ADDER_OF
  Multiplexer #(.width(64)) multiplexer_1 (.in0(multiplexer_2_out), .in1(Q), .out(multiplexer_1_out), .sel(in_3));
  Multiplexer #(.width(64)) multiplexer_2 (
    .in0(adder_64_1_s), .in1({Q[63:32], I_low32}), .out(multiplexer_2_out), .sel(PC_load));
endmodule

module CU_64 (
  input  [31:0] IR_high32,
  input  [3:0] Flag_in,
  output RegWrite,
  output MemRead,
  output OutEnable,
  output OP0,
  output OP1,
  output MemWrite,
  output PC_load,
  output LDA,
  output [4:0] rd,
  output [4:0] rs1,
  output [4:0] rs2
);

  wire add, AN, and_1_out, and_2_out, and_3_out, and_4_out, and_5_out, and_6_out, and_7_out, and_8_out, CMP,
       JC, JMP, JN, JNC, JNO, JNZ, JO, JP, JZ, not_1_out, not_2_out, not_3_out, not_4_out, RO, SUB;
  wire [2:0] rd_t, rs1_t, rs2_t;

  CU_R_LDA cu_r_lda_1 (.I(IR_high32), .R_LDA(LDA), .rd({rd[0], rd[1], rd[2], rd[3], rd[4], rd_t}));  // open: rs1, rs2
  CU_R_ADD cu_r_add_1 (
    .I(IR_high32), .R_ADD(add), .rd({rd[0], rd[1], rd[2], rd[3], rd[4], rd_t}),
    .rs1({rs1[0], rs1[1], rs1[2], rs1[3], rs1[4], rs1_t}),
    .rs2({rs2[0], rs2[1], rs2[2], rs2[3], rs2[4], rs2_t}));
  CU_R_OUT cu_r_out_1 (
    .I(IR_high32), .R_OUT(OutEnable), .rd({rd[0], rd[1], rd[2], rd[3], rd[4], rd_t}),
    .rs1({rs1[0], rs1[1], rs1[2], rs1[3], rs1[4], rs1_t}),
    .rs2({rs2[0], rs2[1], rs2[2], rs2[3], rs2[4], rs2_t}));
  CU_R_JMP cu_r_jmp_1 (.I(IR_high32), .R_JMP(JMP));  // open: rd, rs1, rs2
  CU_R_STA cu_r_sta_1 (
    .I(IR_high32), .R_STA(MemWrite), .rs1({rs1[0], rs1[1], rs1[2], rs1[3], rs1[4], rs1_t}));  // open: rd, rs2
  CU_R_SUB cu_r_sub_1 (
    .I(IR_high32), .R_SUB(SUB), .rd({rd[0], rd[1], rd[2], rd[3], rd[4], rd_t}),
    .rs1({rs1[0], rs1[1], rs1[2], rs1[3], rs1[4], rs1_t}),
    .rs2({rs2[0], rs2[1], rs2[2], rs2[3], rs2[4], rs2_t}));
  CU_R_AND cu_r_and_1 (
    .I(IR_high32), .R_AND(AN), .rd({rd[0], rd[1], rd[2], rd[3], rd[4], rd_t}),
    .rs1({rs1[0], rs1[1], rs1[2], rs1[3], rs1[4], rs1_t}),
    .rs2({rs2[0], rs2[1], rs2[2], rs2[3], rs2[4], rs2_t}));
  CU_R_OR cu_r_or_1 (
    .I(IR_high32), .R_OR(RO), .rd({rd[0], rd[1], rd[2], rd[3], rd[4], rd_t}),
    .rs1({rs1[0], rs1[1], rs1[2], rs1[3], rs1[4], rs1_t}),
    .rs2({rs2[0], rs2[1], rs2[2], rs2[3], rs2[4], rs2_t}));
  CU_R_JZ cu_r_jz_1 (.I(IR_high32), .R_JZ(JZ));  // open: rd, rs1, rs2
  CU_R_JNZ cu_r_jnz_1 (.I(IR_high32), .R_JNZ(JNZ));  // open: rd, rs1, rs2
  CU_R_JC cu_r_jc_1 (.I(IR_high32), .R_JC(JC));  // open: rd, rs1, rs2
  CU_R_JNC cu_r_jnc_1 (.I(IR_high32), .R_JNC(JNC));  // open: rd, rs1, rs2
  CU_R_JN cu_r_jn_1 (.I(IR_high32), .R_JN(JN));  // open: rd, rs1, rs2
  CU_R_JP cu_r_jp_1 (.I(IR_high32), .R_JP(JP));  // open: rd, rs1, rs2
  CU_R_JO cu_r_jo_1 (.I(IR_high32), .R_JO(JO));  // open: rd, rs1, rs2
  CU_R_JNO cu_r_jno_1 (.I(IR_high32), .R_JNO(JNO));  // open: rd, rs1, rs2
  CU_R_CMP cu_r_cmp_1 (
    .I(IR_high32), .R_CMP(CMP), .rs1({rs1[0], rs1[1], rs1[2], rs1[3], rs1[4], rs1_t}),
    .rs2({rs2[0], rs2[1], rs2[2], rs2[3], rs2[4], rs2_t}));  // open: rd
  or or_1 (MemRead, LDA, SUB, AN, RO, add);
  or or_2 (OP0, SUB, CMP, RO);
  or or_3 (OP1, AN, RO);
  not not_1 (not_1_out, Flag_in[2]);
  not not_2 (not_2_out, Flag_in[0]);
  not not_3 (not_3_out, Flag_in[3]);
  not not_4 (not_4_out, Flag_in[1]);
  and and_1 (and_1_out, JZ, Flag_in[2]);
  and and_2 (and_2_out, JNZ, not_1_out);
  and and_3 (and_3_out, JC, Flag_in[0]);
  and and_4 (and_4_out, JNC, not_2_out);
  and and_5 (and_5_out, JN, Flag_in[3]);
  and and_6 (and_6_out, JP, not_3_out);
  and and_7 (and_7_out, JO, Flag_in[1]);
  and and_8 (and_8_out, JNO, not_4_out);
  or or_4 (PC_load, and_1_out, and_2_out, and_3_out, and_4_out, JMP, and_5_out, and_6_out, and_7_out, and_8_out);

  assign RegWrite = MemRead;

  // Other names for the same wires on the sheet: Flag_CF = Flag_in[0]; Flag_OF = Flag_in[1]; Flag_ZF = Flag_in[2];
  //   Flag_SF = Flag_in[3]; ir[31:0] = IR_high32; out_64 = OutEnable; rd_t[7:3] = {rd[0], rd[1], rd[2], rd[3], rd[4]};
  //   rs1_t[7:3] = {rs1[0], rs1[1], rs1[2], rs1[3], rs1[4]}; rs2_t[7:3] = {rs2[0], rs2[1], rs2[2], rs2[3], rs2[4]};
  //   STA = MemWrite
endmodule

module CPU_64 (
  input  [63:0] in_1,
  input  Clock,
  output [63:0] Read,
  output [63:0] CPU_out,
  output MemRead,
  output MemWrite,
  output [63:0] MemWrite_Data
);

  wire LDA, or_1_out, or_2_out, or_3_out, OutEnable, PC_load, RegWrite;
  wire [1:0] OP;
  wire [3:0] alu_64_1_cf, register_1_q;
  wire [4:0] cu_64_1_rd, rs1, rs2;
  wire [31:0] IR_high32, IR_low32;
  wire [63:0] multiplexer_2_out, pc_64_1_q, RD, reg_file_32x64_1_rs2_out, rs1_out;

  or or_1 (or_1_out, LDA, MemWrite);
  PC_64 pc_64_1 (.Clock(Clock), .PC_load(PC_load), .in_3(or_1_out), .I_low32(IR_low32), .Q(pc_64_1_q));
  Multiplexer #(.width(64)) multiplexer_1 (.in0(pc_64_1_q), .in1({{32{1'b0}}, IR_low32}), .out(Read), .sel(or_2_out));
  or or_2 (or_2_out, LDA, MemWrite);
  Multiplexer #(.width(64)) multiplexer_2 (.in0(in_1), .in1({64{1'b0}}), .out(multiplexer_2_out), .sel(or_3_out));
  or or_3 (or_3_out, LDA, MemWrite);
  IR_64 ir_64_1 (.D(multiplexer_2_out), .Clock(Clock), .Q({IR_high32, IR_low32}));
  CU_64 cu_64_1 (
    .IR_high32(IR_high32), .Flag_in(register_1_q), .RegWrite(RegWrite), .MemRead(MemRead),
    .OutEnable(OutEnable), .OP0(OP[0]), .OP1(OP[1]), .MemWrite(MemWrite), .PC_load(PC_load), .LDA(LDA),
    .rd(cu_64_1_rd), .rs1(rs1), .rs2(rs2));
  assign MemWrite_Data = MemWrite ? rs1_out : 64'bz;  // Controlled_Buffer controlled_buffer_1
  REG_FILE_32x64 reg_file_32x64_1 (
    .rs1(rs1), .rs2(rs2), .D(RD), .RegWrite(RegWrite), .REG_OP(cu_64_1_rd), .Clock(Clock), .rs1_out(rs1_out),
    .rs2_out(reg_file_32x64_1_rs2_out));
  assign CPU_out = OutEnable ? rs1_out : 64'bz;  // Controlled_Buffer controlled_buffer_2
  ALU_64 alu_64_1 (
    .A(rs1_out), .B(reg_file_32x64_1_rs2_out), .OP(OP), .LDA_data(in_1), .LDA(LDA), .R(RD),
    .CF(alu_64_1_cf[0]), .ALU_OF(alu_64_1_cf[1]), .ZF(alu_64_1_cf[2]), .SF(alu_64_1_cf[3]));
  Register #(.width(4)) register_1 (.D(alu_64_1_cf), .en(1'b1), .clk(Clock), .Q(register_1_q));  // open: clr

  // Other names for the same wires on the sheet: LDA_data[63:0] = in_1
endmodule

module REG_FILE_32x64 (
  input  [4:0] rs1,
  input  [4:0] rs2,
  input  [63:0] D,
  input  RegWrite,
  input  [4:0] REG_OP,
  input  Clock,
  output [63:0] rs1_out,
  output [63:0] rs2_out
);

  wire [31:0] decoder_1_out0;
  wire [63:0] multiplexer_1_out, multiplexer_2_out, multiplexer_3_out, multiplexer_4_out, multiplexer_5_out,
       multiplexer_6_out, multiplexer_7_out, multiplexer_8_out, multiplexer_9_out, multiplexer_10_out,
       multiplexer_11_out, multiplexer_12_out, multiplexer_13_out, multiplexer_14_out, multiplexer_15_out,
       multiplexer_16_out, multiplexer_17_out, multiplexer_18_out, multiplexer_19_out, multiplexer_20_out,
       multiplexer_21_out, multiplexer_22_out, multiplexer_23_out, multiplexer_24_out, multiplexer_25_out,
       multiplexer_26_out, multiplexer_27_out, multiplexer_28_out, multiplexer_29_out, multiplexer_30_out,
       multiplexer_31_out, multiplexer_32_out, Q0, Q1, Q2, Q3, Q4, Q5, Q6, Q7, Q8, Q9, Q10, Q11, Q12, Q13,
       Q14, Q15, Q16, Q17, Q18, Q19, Q20, Q21, Q22, Q23, Q24, Q25, Q26, Q27, Q28, Q29, Q30, Q31;

  Decoder #(.select(5)) decoder_1 (
    .out0(decoder_1_out0[0]), .out1(decoder_1_out0[1]), .out2(decoder_1_out0[2]), .out3(decoder_1_out0[3]),
    .out4(decoder_1_out0[4]), .out5(decoder_1_out0[5]), .out6(decoder_1_out0[6]), .out7(decoder_1_out0[7]),
    .out8(decoder_1_out0[8]), .out9(decoder_1_out0[9]), .out10(decoder_1_out0[10]),
    .out11(decoder_1_out0[11]), .out12(decoder_1_out0[12]), .out13(decoder_1_out0[13]),
    .out14(decoder_1_out0[14]), .out15(decoder_1_out0[15]), .out16(decoder_1_out0[16]),
    .out17(decoder_1_out0[17]), .out18(decoder_1_out0[18]), .out19(decoder_1_out0[19]),
    .out20(decoder_1_out0[20]), .out21(decoder_1_out0[21]), .out22(decoder_1_out0[22]),
    .out23(decoder_1_out0[23]), .out24(decoder_1_out0[24]), .out25(decoder_1_out0[25]),
    .out26(decoder_1_out0[26]), .out27(decoder_1_out0[27]), .out28(decoder_1_out0[28]),
    .out29(decoder_1_out0[29]), .out30(decoder_1_out0[30]), .out31(decoder_1_out0[31]), .sel(REG_OP),
    .en(RegWrite));
  Register #(.width(64)) register_1 (.D(multiplexer_1_out), .en(decoder_1_out0[0]), .clk(Clock), .Q(Q0));  // open: clr
  Multiplexer #(.width(64)) multiplexer_1 (.in0(Q0), .in1(D), .out(multiplexer_1_out), .sel(decoder_1_out0[0]));
  Register #(.width(64)) register_2 (.D(multiplexer_2_out), .en(decoder_1_out0[1]), .clk(Clock), .Q(Q1));  // open: clr
  Multiplexer #(.width(64)) multiplexer_2 (.in0(Q1), .in1(D), .out(multiplexer_2_out), .sel(decoder_1_out0[1]));
  Register #(.width(64)) register_3 (.D(multiplexer_3_out), .en(decoder_1_out0[2]), .clk(Clock), .Q(Q2));  // open: clr
  Multiplexer #(.width(64)) multiplexer_3 (.in0(Q2), .in1(D), .out(multiplexer_3_out), .sel(decoder_1_out0[2]));
  Register #(.width(64)) register_4 (.D(multiplexer_4_out), .en(decoder_1_out0[3]), .clk(Clock), .Q(Q3));  // open: clr
  Multiplexer #(.width(64)) multiplexer_4 (.in0(Q3), .in1(D), .out(multiplexer_4_out), .sel(decoder_1_out0[3]));
  Register #(.width(64)) register_5 (.D(multiplexer_5_out), .en(decoder_1_out0[4]), .clk(Clock), .Q(Q4));  // open: clr
  Multiplexer #(.width(64)) multiplexer_5 (.in0(Q4), .in1(D), .out(multiplexer_5_out), .sel(decoder_1_out0[4]));
  Register #(.width(64)) register_6 (.D(multiplexer_6_out), .en(decoder_1_out0[5]), .clk(Clock), .Q(Q5));  // open: clr
  Multiplexer #(.width(64)) multiplexer_6 (.in0(Q5), .in1(D), .out(multiplexer_6_out), .sel(decoder_1_out0[5]));
  Register #(.width(64)) register_7 (.D(multiplexer_7_out), .en(decoder_1_out0[6]), .clk(Clock), .Q(Q6));  // open: clr
  Multiplexer #(.width(64)) multiplexer_7 (.in0(Q6), .in1(D), .out(multiplexer_7_out), .sel(decoder_1_out0[6]));
  Register #(.width(64)) register_8 (.D(multiplexer_8_out), .en(decoder_1_out0[7]), .clk(Clock), .Q(Q7));  // open: clr
  Multiplexer #(.width(64)) multiplexer_8 (.in0(Q7), .in1(D), .out(multiplexer_8_out), .sel(decoder_1_out0[7]));
  Register #(.width(64)) register_9 (.D(multiplexer_9_out), .en(decoder_1_out0[8]), .clk(Clock), .Q(Q8));  // open: clr
  Multiplexer #(.width(64)) multiplexer_9 (.in0(Q8), .in1(D), .out(multiplexer_9_out), .sel(decoder_1_out0[8]));
  Register #(.width(64)) register_10 (
    .D(multiplexer_10_out), .en(decoder_1_out0[9]), .clk(Clock), .Q(Q9));  // open: clr
  Multiplexer #(.width(64)) multiplexer_10 (.in0(Q9), .in1(D), .out(multiplexer_10_out), .sel(decoder_1_out0[9]));
  Register #(.width(64)) register_11 (
    .D(multiplexer_11_out), .en(decoder_1_out0[10]), .clk(Clock), .Q(Q10));  // open: clr
  Multiplexer #(.width(64)) multiplexer_11 (.in0(Q10), .in1(D), .out(multiplexer_11_out), .sel(decoder_1_out0[10]));
  Register #(.width(64)) register_12 (
    .D(multiplexer_12_out), .en(decoder_1_out0[11]), .clk(Clock), .Q(Q11));  // open: clr
  Multiplexer #(.width(64)) multiplexer_12 (.in0(Q11), .in1(D), .out(multiplexer_12_out), .sel(decoder_1_out0[11]));
  Register #(.width(64)) register_13 (
    .D(multiplexer_13_out), .en(decoder_1_out0[12]), .clk(Clock), .Q(Q12));  // open: clr
  Multiplexer #(.width(64)) multiplexer_13 (.in0(Q12), .in1(D), .out(multiplexer_13_out), .sel(decoder_1_out0[12]));
  Register #(.width(64)) register_14 (
    .D(multiplexer_14_out), .en(decoder_1_out0[13]), .clk(Clock), .Q(Q13));  // open: clr
  Multiplexer #(.width(64)) multiplexer_14 (.in0(Q13), .in1(D), .out(multiplexer_14_out), .sel(decoder_1_out0[13]));
  Register #(.width(64)) register_15 (
    .D(multiplexer_15_out), .en(decoder_1_out0[14]), .clk(Clock), .Q(Q14));  // open: clr
  Multiplexer #(.width(64)) multiplexer_15 (.in0(Q14), .in1(D), .out(multiplexer_15_out), .sel(decoder_1_out0[14]));
  Register #(.width(64)) register_16 (
    .D(multiplexer_16_out), .en(decoder_1_out0[15]), .clk(Clock), .Q(Q15));  // open: clr
  Multiplexer #(.width(64)) multiplexer_16 (.in0(Q15), .in1(D), .out(multiplexer_16_out), .sel(decoder_1_out0[15]));
  Register #(.width(64)) register_17 (
    .D(multiplexer_17_out), .en(decoder_1_out0[16]), .clk(Clock), .Q(Q16));  // open: clr
  Multiplexer #(.width(64)) multiplexer_17 (.in0(Q16), .in1(D), .out(multiplexer_17_out), .sel(decoder_1_out0[16]));
  Register #(.width(64)) register_18 (
    .D(multiplexer_18_out), .en(decoder_1_out0[17]), .clk(Clock), .Q(Q17));  // open: clr
  Multiplexer #(.width(64)) multiplexer_18 (.in0(Q17), .in1(D), .out(multiplexer_18_out), .sel(decoder_1_out0[17]));
  Register #(.width(64)) register_19 (
    .D(multiplexer_19_out), .en(decoder_1_out0[18]), .clk(Clock), .Q(Q18));  // open: clr
  Multiplexer #(.width(64)) multiplexer_19 (.in0(Q18), .in1(D), .out(multiplexer_19_out), .sel(decoder_1_out0[18]));
  Register #(.width(64)) register_20 (
    .D(multiplexer_20_out), .en(decoder_1_out0[19]), .clk(Clock), .Q(Q19));  // open: clr
  Multiplexer #(.width(64)) multiplexer_20 (.in0(Q19), .in1(D), .out(multiplexer_20_out), .sel(decoder_1_out0[19]));
  Register #(.width(64)) register_21 (
    .D(multiplexer_21_out), .en(decoder_1_out0[20]), .clk(Clock), .Q(Q20));  // open: clr
  Multiplexer #(.width(64)) multiplexer_21 (.in0(Q20), .in1(D), .out(multiplexer_21_out), .sel(decoder_1_out0[20]));
  Register #(.width(64)) register_22 (
    .D(multiplexer_22_out), .en(decoder_1_out0[21]), .clk(Clock), .Q(Q21));  // open: clr
  Multiplexer #(.width(64)) multiplexer_22 (.in0(Q21), .in1(D), .out(multiplexer_22_out), .sel(decoder_1_out0[21]));
  Register #(.width(64)) register_23 (
    .D(multiplexer_23_out), .en(decoder_1_out0[22]), .clk(Clock), .Q(Q22));  // open: clr
  Multiplexer #(.width(64)) multiplexer_23 (.in0(Q22), .in1(D), .out(multiplexer_23_out), .sel(decoder_1_out0[22]));
  Register #(.width(64)) register_24 (
    .D(multiplexer_24_out), .en(decoder_1_out0[23]), .clk(Clock), .Q(Q23));  // open: clr
  Multiplexer #(.width(64)) multiplexer_24 (.in0(Q23), .in1(D), .out(multiplexer_24_out), .sel(decoder_1_out0[23]));
  Register #(.width(64)) register_25 (
    .D(multiplexer_25_out), .en(decoder_1_out0[24]), .clk(Clock), .Q(Q24));  // open: clr
  Multiplexer #(.width(64)) multiplexer_25 (.in0(Q24), .in1(D), .out(multiplexer_25_out), .sel(decoder_1_out0[24]));
  Register #(.width(64)) register_26 (
    .D(multiplexer_26_out), .en(decoder_1_out0[25]), .clk(Clock), .Q(Q25));  // open: clr
  Multiplexer #(.width(64)) multiplexer_26 (.in0(Q25), .in1(D), .out(multiplexer_26_out), .sel(decoder_1_out0[25]));
  Register #(.width(64)) register_27 (
    .D(multiplexer_27_out), .en(decoder_1_out0[26]), .clk(Clock), .Q(Q26));  // open: clr
  Multiplexer #(.width(64)) multiplexer_27 (.in0(Q26), .in1(D), .out(multiplexer_27_out), .sel(decoder_1_out0[26]));
  Register #(.width(64)) register_28 (
    .D(multiplexer_28_out), .en(decoder_1_out0[27]), .clk(Clock), .Q(Q27));  // open: clr
  Multiplexer #(.width(64)) multiplexer_28 (.in0(Q27), .in1(D), .out(multiplexer_28_out), .sel(decoder_1_out0[27]));
  Register #(.width(64)) register_29 (
    .D(multiplexer_29_out), .en(decoder_1_out0[28]), .clk(Clock), .Q(Q28));  // open: clr
  Multiplexer #(.width(64)) multiplexer_29 (.in0(Q28), .in1(D), .out(multiplexer_29_out), .sel(decoder_1_out0[28]));
  Register #(.width(64)) register_30 (
    .D(multiplexer_30_out), .en(decoder_1_out0[29]), .clk(Clock), .Q(Q29));  // open: clr
  Multiplexer #(.width(64)) multiplexer_30 (.in0(Q29), .in1(D), .out(multiplexer_30_out), .sel(decoder_1_out0[29]));
  Register #(.width(64)) register_31 (
    .D(multiplexer_31_out), .en(decoder_1_out0[30]), .clk(Clock), .Q(Q30));  // open: clr
  Multiplexer #(.width(64)) multiplexer_31 (.in0(Q30), .in1(D), .out(multiplexer_31_out), .sel(decoder_1_out0[30]));
  Register #(.width(64)) register_32 (
    .D(multiplexer_32_out), .en(decoder_1_out0[31]), .clk(Clock), .Q(Q31));  // open: clr
  Multiplexer #(.width(64)) multiplexer_32 (.in0(Q31), .in1(D), .out(multiplexer_32_out), .sel(decoder_1_out0[31]));
  Multiplexer #(.select(5), .width(64)) multiplexer_33 (
    .in0(Q0), .in1(Q1), .in2(Q2), .in3(Q3), .in4(Q4), .in5(Q5), .in6(Q6), .in7(Q7), .in8(Q8), .in9(Q9),
    .in10(Q10), .in11(Q11), .in12(Q12), .in13(Q13), .in14(Q14), .in15(Q15), .in16(Q16), .in17(Q17),
    .in18(Q18), .in19(Q19), .in20(Q20), .in21(Q21), .in22(Q22), .in23(Q23), .in24(Q24), .in25(Q25),
    .in26(Q26), .in27(Q27), .in28(Q28), .in29(Q29), .in30(Q30), .in31(Q31), .out(rs2_out), .sel(rs2));
  Multiplexer #(.select(5), .width(64)) multiplexer_34 (
    .in0(Q0), .in1(Q1), .in2(Q2), .in3(Q3), .in4(Q4), .in5(Q5), .in6(Q6), .in7(Q7), .in8(Q8), .in9(Q9),
    .in10(Q10), .in11(Q11), .in12(Q12), .in13(Q13), .in14(Q14), .in15(Q15), .in16(Q16), .in17(Q17),
    .in18(Q18), .in19(Q19), .in20(Q20), .in21(Q21), .in22(Q22), .in23(Q23), .in24(Q24), .in25(Q25),
    .in26(Q26), .in27(Q27), .in28(Q28), .in29(Q29), .in30(Q30), .in31(Q31), .out(rs1_out), .sel(rs1));
endmodule

module CU_R_ADD (
  input  [31:0] I,
  output R_ADD,
  output [7:0] rd,
  output [7:0] rs1,
  output [7:0] rs2
);

  wire [6:0] not_1_out;

  not not_1 (not_1_out[0], I[31]);
  not not_2 (not_1_out[1], I[30]);
  not not_3 (not_1_out[2], I[29]);
  not not_4 (not_1_out[4], I[27]);
  not not_5 (not_1_out[5], I[26]);
  not not_6 (not_1_out[6], I[25]);
  and and_1 (R_ADD, not_1_out[0], not_1_out[1], not_1_out[2], I[28], not_1_out[4], not_1_out[5], not_1_out[6], I[24], 1'b1);

  assign rd = {I[16], I[17], I[18], I[19], I[20], I[21], I[22], I[23]};
  assign rs1 = {I[8], I[9], I[10], I[11], I[12], I[13], I[14], I[15]};
  assign rs2 = {I[0], I[1], I[2], I[3], I[4], I[5], I[6], I[7]};
endmodule

module CU_R_SUB (
  input  [31:0] I,
  output R_SUB,
  output [7:0] rd,
  output [7:0] rs1,
  output [7:0] rs2
);

  wire [7:0] not_1_out;

  not not_1 (not_1_out[0], I[31]);
  not not_2 (not_1_out[1], I[30]);
  not not_3 (not_1_out[2], I[29]);
  not not_4 (not_1_out[4], I[27]);
  not not_5 (not_1_out[5], I[26]);
  not not_6 (not_1_out[7], I[24]);
  and and_1 (R_SUB, not_1_out[0], not_1_out[1], not_1_out[2], I[28], not_1_out[4], not_1_out[5], I[25], not_1_out[7], 1'b1);

  assign rd = {I[16], I[17], I[18], I[19], I[20], I[21], I[22], I[23]};
  assign rs1 = {I[8], I[9], I[10], I[11], I[12], I[13], I[14], I[15]};
  assign rs2 = {I[0], I[1], I[2], I[3], I[4], I[5], I[6], I[7]};
endmodule

module CU_R_AND (
  input  [31:0] I,
  output R_AND,
  output [7:0] rd,
  output [7:0] rs1,
  output [7:0] rs2
);

  wire [5:0] not_1_out;

  not not_1 (not_1_out[0], I[31]);
  not not_2 (not_1_out[1], I[30]);
  not not_3 (not_1_out[2], I[29]);
  not not_4 (not_1_out[4], I[27]);
  not not_5 (not_1_out[5], I[26]);
  and and_1 (R_AND, not_1_out[0], not_1_out[1], not_1_out[2], I[28], not_1_out[4], not_1_out[5], I[25], I[24], 1'b1);

  assign rd = {I[16], I[17], I[18], I[19], I[20], I[21], I[22], I[23]};
  assign rs1 = {I[8], I[9], I[10], I[11], I[12], I[13], I[14], I[15]};
  assign rs2 = {I[0], I[1], I[2], I[3], I[4], I[5], I[6], I[7]};
endmodule

module CU_R_OR (
  input  [31:0] I,
  output R_OR,
  output [7:0] rd,
  output [7:0] rs1,
  output [7:0] rs2
);

  wire [7:0] not_1_out;

  not not_1 (not_1_out[0], I[31]);
  not not_2 (not_1_out[1], I[30]);
  not not_3 (not_1_out[2], I[29]);
  not not_4 (not_1_out[4], I[27]);
  not not_5 (not_1_out[6], I[25]);
  not not_6 (not_1_out[7], I[24]);
  and and_1 (R_OR, not_1_out[0], not_1_out[1], not_1_out[2], I[28], not_1_out[4], I[26], not_1_out[6], not_1_out[7], 1'b1);

  assign rs1 = {I[8], I[9], I[10], I[11], I[12], I[13], I[14], I[15]};
  assign rs2 = {I[0], I[1], I[2], I[3], I[4], I[5], I[6], I[7]};
endmodule

module CU_R_LDA (
  input  [31:0] I,
  output R_LDA,
  output [7:0] rd,
  output [7:0] rs1,
  output [7:0] rs2
);

  wire [6:0] not_1_out;

  not not_1 (not_1_out[0], I[31]);
  not not_2 (not_1_out[1], I[30]);
  not not_3 (not_1_out[2], I[29]);
  not not_4 (not_1_out[3], I[28]);
  not not_5 (not_1_out[4], I[27]);
  not not_6 (not_1_out[5], I[26]);
  not not_7 (not_1_out[6], I[25]);
  and and_1 (R_LDA, not_1_out[0], not_1_out[1], not_1_out[2], not_1_out[3], not_1_out[4], not_1_out[5], not_1_out[6], I[24], 1'b1);
endmodule

module CU_R_OUT (
  input  [31:0] I,
  output R_OUT,
  output [7:0] rd,
  output [7:0] rs1,
  output [7:0] rs2
);

  wire [7:0] not_1_out;

  not not_1 (not_1_out[0], I[31]);
  not not_2 (not_1_out[1], I[30]);
  not not_3 (not_1_out[2], I[29]);
  not not_4 (not_1_out[3], I[28]);
  not not_5 (not_1_out[7], I[24]);
  and and_1 (R_OUT, not_1_out[0], not_1_out[1], not_1_out[2], not_1_out[3], I[27], I[26], I[25], not_1_out[7], 1'b1);

  assign rd = {I[16], I[17], I[18], I[19], I[20], I[21], I[22], I[23]};
  assign rs1 = {I[8], I[9], I[10], I[11], I[12], I[13], I[14], I[15]};
  assign rs2 = {I[0], I[1], I[2], I[3], I[4], I[5], I[6], I[7]};
endmodule

module CU_R_STA (
  input  [31:0] I,
  output R_STA,
  output [7:0] rd,
  output [7:0] rs1,
  output [7:0] rs2
);

  wire [5:0] not_1_out;

  not not_1 (not_1_out[0], I[31]);
  not not_2 (not_1_out[1], I[30]);
  not not_3 (not_1_out[2], I[29]);
  not not_4 (not_1_out[3], I[28]);
  not not_5 (not_1_out[4], I[27]);
  not not_6 (not_1_out[5], I[26]);
  and and_1 (R_STA, not_1_out[0], not_1_out[1], not_1_out[2], not_1_out[3], not_1_out[4], not_1_out[5], I[25], I[24], 1'b1);
endmodule

module CU_R_JMP (
  input  [31:0] I,
  output R_JMP,
  output [7:0] rd,
  output [7:0] rs1,
  output [7:0] rs2
);

  wire [7:0] not_1_out;

  not not_1 (not_1_out[0], I[31]);
  not not_2 (not_1_out[1], I[30]);
  not not_3 (not_1_out[2], I[29]);
  not not_4 (not_1_out[3], I[28]);
  not not_5 (not_1_out[5], I[26]);
  not not_6 (not_1_out[6], I[25]);
  not not_7 (not_1_out[7], I[24]);
  and and_1 (R_JMP, not_1_out[0], not_1_out[1], not_1_out[2], not_1_out[3], I[27], not_1_out[5], not_1_out[6], not_1_out[7], 1'b1);
endmodule

module CU_R_JZ (
  input  [31:0] I,
  output R_JZ,
  output [7:0] rd,
  output [7:0] rs1,
  output [7:0] rs2
);

  wire [7:0] not_1_out;

  not not_1 (not_1_out[0], I[31]);
  not not_2 (not_1_out[1], I[30]);
  not not_3 (not_1_out[3], I[28]);
  not not_4 (not_1_out[4], I[27]);
  not not_5 (not_1_out[5], I[26]);
  not not_6 (not_1_out[6], I[25]);
  not not_7 (not_1_out[7], I[24]);
  and and_1 (R_JZ, not_1_out[0], not_1_out[1], I[29], not_1_out[3], not_1_out[4], not_1_out[5], not_1_out[6], not_1_out[7], 1'b1);
endmodule

module CU_R_JNZ (
  input  [31:0] I,
  output R_JNZ,
  output [7:0] rd,
  output [7:0] rs1,
  output [7:0] rs2
);

  wire [6:0] not_1_out;

  not not_1 (not_1_out[0], I[31]);
  not not_2 (not_1_out[1], I[30]);
  not not_3 (not_1_out[3], I[28]);
  not not_4 (not_1_out[4], I[27]);
  not not_5 (not_1_out[5], I[26]);
  not not_6 (not_1_out[6], I[25]);
  and and_1 (R_JNZ, not_1_out[0], not_1_out[1], I[29], not_1_out[3], not_1_out[4], not_1_out[5], not_1_out[6], I[24], 1'b1);
endmodule

module CU_R_JC (
  input  [31:0] I,
  output R_JC,
  output [7:0] rd,
  output [7:0] rs1,
  output [7:0] rs2
);

  wire [7:0] not_1_out;

  not not_1 (not_1_out[0], I[31]);
  not not_2 (not_1_out[1], I[30]);
  not not_3 (not_1_out[3], I[28]);
  not not_4 (not_1_out[4], I[27]);
  not not_5 (not_1_out[5], I[26]);
  not not_6 (not_1_out[7], I[24]);
  and and_1 (R_JC, not_1_out[0], not_1_out[1], I[29], not_1_out[3], not_1_out[4], not_1_out[5], I[25], not_1_out[7], 1'b1);
endmodule

module CU_R_JNC (
  input  [31:0] I,
  output R_JNC,
  output [7:0] rd,
  output [7:0] rs1,
  output [7:0] rs2
);

  wire [5:0] not_1_out;

  not not_1 (not_1_out[0], I[31]);
  not not_2 (not_1_out[1], I[30]);
  not not_3 (not_1_out[3], I[28]);
  not not_4 (not_1_out[4], I[27]);
  not not_5 (not_1_out[5], I[26]);
  and and_1 (R_JNC, not_1_out[0], not_1_out[1], I[29], not_1_out[3], not_1_out[4], not_1_out[5], I[25], I[24], 1'b1);
endmodule

module CU_R_JN (
  input  [31:0] I,
  output R_JN,
  output [7:0] rd,
  output [7:0] rs1,
  output [7:0] rs2
);

  wire [7:0] not_1_out;

  not not_1 (not_1_out[0], I[31]);
  not not_2 (not_1_out[1], I[30]);
  not not_3 (not_1_out[3], I[28]);
  not not_4 (not_1_out[4], I[27]);
  not not_5 (not_1_out[6], I[25]);
  not not_6 (not_1_out[7], I[24]);
  and and_1 (R_JN, not_1_out[0], not_1_out[1], I[29], not_1_out[3], not_1_out[4], I[26], not_1_out[6], not_1_out[7], 1'b1);
endmodule

module CU_R_JP (
  input  [31:0] I,
  output R_JP,
  output [7:0] rd,
  output [7:0] rs1,
  output [7:0] rs2
);

  wire [6:0] not_1_out;

  not not_1 (not_1_out[0], I[31]);
  not not_2 (not_1_out[1], I[30]);
  not not_3 (not_1_out[3], I[28]);
  not not_4 (not_1_out[4], I[27]);
  not not_5 (not_1_out[6], I[25]);
  and and_1 (R_JP, not_1_out[0], not_1_out[1], I[29], not_1_out[3], not_1_out[4], I[26], not_1_out[6], I[24], 1'b1);
endmodule

module CU_R_JO (
  input  [31:0] I,
  output R_JO,
  output [7:0] rd,
  output [7:0] rs1,
  output [7:0] rs2
);

  wire [7:0] not_1_out;

  not not_1 (not_1_out[0], I[31]);
  not not_2 (not_1_out[1], I[30]);
  not not_3 (not_1_out[3], I[28]);
  not not_4 (not_1_out[4], I[27]);
  not not_5 (not_1_out[7], I[24]);
  and and_1 (R_JO, not_1_out[0], not_1_out[1], I[29], not_1_out[3], not_1_out[4], I[26], I[25], not_1_out[7], 1'b1);
endmodule

module CU_R_JNO (
  input  [31:0] I,
  output R_JNO,
  output [7:0] rd,
  output [7:0] rs1,
  output [7:0] rs2
);

  wire [4:0] not_1_out;

  not not_1 (not_1_out[0], I[31]);
  not not_2 (not_1_out[1], I[30]);
  not not_3 (not_1_out[3], I[28]);
  not not_4 (not_1_out[4], I[27]);
  and and_1 (R_JNO, not_1_out[0], not_1_out[1], I[29], not_1_out[3], not_1_out[4], I[26], I[25], I[24], 1'b1);
endmodule

module CU_R_CMP (
  input  [31:0] I,
  output R_CMP,
  output [7:0] rd,
  output [7:0] rs1,
  output [7:0] rs2
);

  wire [7:0] not_1_out;

  not not_1 (not_1_out[0], I[31]);
  not not_2 (not_1_out[1], I[30]);
  not not_3 (not_1_out[3], I[28]);
  not not_4 (not_1_out[5], I[26]);
  not not_5 (not_1_out[6], I[25]);
  not not_6 (not_1_out[7], I[24]);
  and and_1 (R_CMP, not_1_out[0], not_1_out[1], I[29], not_1_out[3], I[27], not_1_out[5], not_1_out[6], not_1_out[7], 1'b1);
endmodule
